// Logisim project 32 Bit Extender.circ as structural Verilog: 1 circuit, main circuit main
module main (
  input  [15:0] in_1,
  input  ExtOp,
  output [31:0] out_3
);

  wire [31:0] bit_extender_1_out, bit_extender_2_out;

  assign bit_extender_1_out = {{16{1'b0}}, in_1};  // Bit_Extender bit_extender_1
  assign bit_extender_2_out = {{16{1'b0}}, in_1};  // Bit_Extender bit_extender_2
  Multiplexer #(.width(32)) multiplexer_1 (
    .in0(bit_extender_1_out), .in1(bit_extender_2_out), .out(out_3), .sel(ExtOp));  // open: en

  // Notes on the sheet:
  //   16 Bit Input
  //   32 Bit Output
endmodule
