// Logisim project ALU.circ as structural Verilog: 3 circuits, main circuit main
module main (
  input  [31:0] in_1,
  input  [31:0] in_2,
  input  in_3
);

  wire [31:0] XOR_Gate_out_3;

  _32_bit_And_Gate XOR_Gate (.out_3(XOR_Gate_out_3), .BusB(in_2), .Control_Input(in_3));
  Adder #(.width(32)) adder_1 (.a(in_1), .b(XOR_Gate_out_3), .cout(in_3));  // open: out, cin
endmodule

module _32_bit_And_Gate (
  input  [31:0] BusB,
  input  Control_Input,
  output [31:0] out_3
);

  xor xor_1 (out_3[0], BusB[0], Control_Input);
  xor xor_2 (out_3[1], BusB[1], Control_Input);
  xor xor_3 (out_3[2], BusB[2], Control_Input);
  xor xor_4 (out_3[3], BusB[3], Control_Input);
  xor xor_5 (out_3[4], BusB[4], Control_Input);
  xor xor_6 (out_3[5], BusB[5], Control_Input);
  xor xor_7 (out_3[6], BusB[6], Control_Input);
  xor xor_8 (out_3[7], BusB[7], Control_Input);
  xor xor_9 (out_3[8], BusB[8], Control_Input);
  xor xor_10 (out_3[9], BusB[9], Control_Input);
  xor xor_11 (out_3[10], BusB[10], Control_Input);
  xor xor_12 (out_3[11], BusB[11], Control_Input);
  xor xor_13 (out_3[12], BusB[12], Control_Input);
  xor xor_14 (out_3[13], BusB[13], Control_Input);
  xor xor_15 (out_3[14], BusB[14], Control_Input);
  xor xor_16 (out_3[15], BusB[15], Control_Input);
  xor xor_17 (out_3[16], BusB[16], Control_Input);
  xor xor_18 (out_3[17], BusB[17], Control_Input);
  xor xor_19 (out_3[18], BusB[18], Control_Input);
  xor xor_20 (out_3[19], BusB[19], Control_Input);
  xor xor_21 (out_3[20], BusB[20], Control_Input);
  xor xor_22 (out_3[21], BusB[21], Control_Input);
  xor xor_23 (out_3[22], BusB[22], Control_Input);
  xor xor_24 (out_3[23], BusB[23], Control_Input);
  xor xor_25 (out_3[24], BusB[24], Control_Input);
  xor xor_26 (out_3[25], BusB[25], Control_Input);
  xor xor_27 (out_3[26], BusB[26], Control_Input);
  xor xor_28 (out_3[27], BusB[27], Control_Input);
  xor xor_29 (out_3[28], BusB[28], Control_Input);
  xor xor_30 (out_3[29], BusB[29], Control_Input);
  xor xor_31 (out_3[30], BusB[30], Control_Input);
  xor xor_32 (out_3[31], BusB[31], Control_Input);

  // Notes on the sheet:
  //   1
  //   5
  //   10
  //   15
  //   20
  //   25
endmodule

module Adder_Subtractor (
  input  in_1,
  input  [31:0] A,
  input  [31:0] in_3,
  input  [31:0] in_4,
  output out_5,
  output out_6
);

  wire adder_1_cout, adder_2_cout, adder_3_cout, adder_4_cout, adder_5_cout, adder_6_cout, adder_7_cout,
       adder_8_cout, adder_9_cout, adder_10_cout, adder_11_cout, adder_12_cout, adder_13_cout, adder_14_cout,
       adder_15_cout, adder_16_cout, adder_17_cout, adder_18_cout, adder_19_cout, adder_20_cout,
       adder_21_cout, adder_22_cout, adder_23_cout, adder_24_cout, adder_25_cout, adder_26_cout,
       adder_27_cout, adder_28_cout, adder_29_cout, adder_30_cout, adder_31_cout, and_1_out, and_2_out,
       not_1_out, not_2_out, not_3_out, xor_1_out, xor_2_out, xor_3_out, xor_4_out, xor_5_out, xor_6_out,
       xor_7_out, xor_8_out, xor_9_out, xor_10_out, xor_11_out, xor_12_out, xor_13_out, xor_14_out,
       xor_15_out, xor_16_out, xor_17_out, xor_18_out, xor_19_out, xor_20_out, xor_21_out, xor_22_out,
       xor_23_out, xor_24_out, xor_25_out, xor_26_out, xor_27_out, xor_28_out, xor_29_out, xor_30_out,
       xor_31_out, xor_32_out;

  xor xor_1 (xor_1_out, in_1, in_4[31]);
  xor xor_2 (xor_2_out, in_1, in_4[30]);
  xor xor_3 (xor_3_out, in_1, in_4[29]);
  xor xor_4 (xor_4_out, in_1, in_4[28]);
  xor xor_5 (xor_5_out, in_1, in_4[27]);
  xor xor_6 (xor_6_out, in_1, in_4[26]);
  xor xor_7 (xor_7_out, in_1, in_4[25]);
  xor xor_8 (xor_8_out, in_1, in_4[24]);
  xor xor_9 (xor_9_out, in_1, in_4[23]);
  xor xor_10 (xor_10_out, in_1, in_4[22]);
  xor xor_11 (xor_11_out, in_1, in_4[21]);
  xor xor_12 (xor_12_out, in_1, in_4[20]);
  xor xor_13 (xor_13_out, in_1, in_4[19]);
  xor xor_14 (xor_14_out, in_1, in_4[18]);
  xor xor_15 (xor_15_out, in_1, in_4[17]);
  xor xor_16 (xor_16_out, in_1, in_4[16]);
  xor xor_17 (xor_17_out, in_1, in_4[15]);
  xor xor_18 (xor_18_out, in_1, in_4[14]);
  xor xor_19 (xor_19_out, in_1, in_4[13]);
  xor xor_20 (xor_20_out, in_1, in_4[12]);
  xor xor_21 (xor_21_out, in_1, in_4[11]);
  xor xor_22 (xor_22_out, in_1, in_4[10]);
  xor xor_23 (xor_23_out, in_1, in_4[9]);
  xor xor_24 (xor_24_out, in_1, in_4[8]);
  xor xor_25 (xor_25_out, in_1, in_4[7]);
  xor xor_26 (xor_26_out, in_1, in_4[6]);
  xor xor_27 (xor_27_out, in_1, in_4[5]);
  xor xor_28 (xor_28_out, in_1, in_4[4]);
  xor xor_29 (xor_29_out, in_1, in_4[3]);
  xor xor_30 (xor_30_out, in_1, in_4[2]);
  xor xor_31 (xor_31_out, in_1, in_4[1]);
  xor xor_32 (xor_32_out, in_1, in_4[0]);
  not not_1 (not_1_out, xor_32_out);
  not not_2 (not_2_out, A[31]);
  Adder #(.width(1)) adder_1 (.a(A[0]), .b(xor_1_out), .out(in_3[0]), .cin(in_1), .cout(adder_1_cout));
  Adder #(.width(1)) adder_2 (.a(A[1]), .b(xor_2_out), .out(in_3[1]), .cin(adder_1_cout), .cout(adder_2_cout));
  Adder #(.width(1)) adder_3 (.a(A[2]), .b(xor_3_out), .out(in_3[2]), .cin(adder_2_cout), .cout(adder_3_cout));
  Adder #(.width(1)) adder_4 (.a(A[3]), .b(xor_4_out), .out(in_3[3]), .cin(adder_3_cout), .cout(adder_4_cout));
  Adder #(.width(1)) adder_5 (.a(A[4]), .b(xor_5_out), .out(in_3[4]), .cin(adder_4_cout), .cout(adder_5_cout));
  Adder #(.width(1)) adder_6 (.a(A[5]), .b(xor_6_out), .out(in_3[5]), .cin(adder_5_cout), .cout(adder_6_cout));
  Adder #(.width(1)) adder_7 (.a(A[6]), .b(xor_7_out), .out(in_3[6]), .cin(adder_6_cout), .cout(adder_7_cout));
  Adder #(.width(1)) adder_8 (.a(A[7]), .b(xor_8_out), .out(in_3[7]), .cin(adder_7_cout), .cout(adder_8_cout));
  Adder #(.width(1)) adder_9 (.a(A[8]), .b(xor_9_out), .out(in_3[8]), .cin(adder_8_cout), .cout(adder_9_cout));
  Adder #(.width(1)) adder_10 (.a(A[9]), .b(xor_10_out), .out(in_3[9]), .cin(adder_9_cout), .cout(adder_10_cout));
  Adder #(.width(1)) adder_11 (.a(A[10]), .b(xor_11_out), .out(in_3[10]), .cin(adder_10_cout), .cout(adder_11_cout));
  Adder #(.width(1)) adder_12 (.a(A[11]), .b(xor_12_out), .out(in_3[11]), .cin(adder_11_cout), .cout(adder_12_cout));
  Adder #(.width(1)) adder_13 (.a(A[12]), .b(xor_13_out), .out(in_3[12]), .cin(adder_12_cout), .cout(adder_13_cout));
  Adder #(.width(1)) adder_14 (.a(A[13]), .b(xor_14_out), .out(in_3[13]), .cin(adder_13_cout), .cout(adder_14_cout));
  Adder #(.width(1)) adder_15 (.a(A[14]), .b(xor_15_out), .out(in_3[14]), .cin(adder_14_cout), .cout(adder_15_cout));
  Adder #(.width(1)) adder_16 (.a(A[15]), .b(xor_16_out), .out(in_3[15]), .cin(adder_15_cout), .cout(adder_16_cout));
  Adder #(.width(1)) adder_17 (.a(A[16]), .b(xor_17_out), .out(in_3[16]), .cin(adder_16_cout), .cout(adder_17_cout));
  Adder #(.width(1)) adder_18 (.a(A[17]), .b(xor_18_out), .out(in_3[17]), .cin(adder_17_cout), .cout(adder_18_cout));
  Adder #(.width(1)) adder_19 (.a(A[18]), .b(xor_19_out), .out(in_3[18]), .cin(adder_18_cout), .cout(adder_19_cout));
  Adder #(.width(1)) adder_20 (.a(A[19]), .b(xor_20_out), .out(in_3[19]), .cin(adder_19_cout), .cout(adder_20_cout));
  Adder #(.width(1)) adder_21 (.a(A[20]), .b(xor_21_out), .out(in_3[20]), .cin(adder_20_cout), .cout(adder_21_cout));
  Adder #(.width(1)) adder_22 (.a(A[21]), .b(xor_22_out), .out(in_3[21]), .cin(adder_21_cout), .cout(adder_22_cout));
  Adder #(.width(1)) adder_23 (.a(A[22]), .b(xor_23_out), .out(in_3[22]), .cin(adder_22_cout), .cout(adder_23_cout));
  Adder #(.width(1)) adder_24 (.a(A[23]), .b(xor_24_out), .out(in_3[23]), .cin(adder_23_cout), .cout(adder_24_cout));
  Adder #(.width(1)) adder_25 (.a(A[24]), .b(xor_25_out), .out(in_3[24]), .cin(adder_24_cout), .cout(adder_25_cout));
  Adder #(.width(1)) adder_26 (.a(A[25]), .b(xor_26_out), .out(in_3[25]), .cin(adder_25_cout), .cout(adder_26_cout));
  Adder #(.width(1)) adder_27 (.a(A[26]), .b(xor_27_out), .out(in_3[26]), .cin(adder_26_cout), .cout(adder_27_cout));
  Adder #(.width(1)) adder_28 (.a(A[27]), .b(xor_28_out), .out(in_3[27]), .cin(adder_27_cout), .cout(adder_28_cout));
  Adder #(.width(1)) adder_29 (.a(A[28]), .b(xor_29_out), .out(in_3[28]), .cin(adder_28_cout), .cout(adder_29_cout));
  Adder #(.width(1)) adder_30 (.a(A[29]), .b(xor_30_out), .out(in_3[29]), .cin(adder_29_cout), .cout(adder_30_cout));
  Adder #(.width(1)) adder_31 (.a(A[30]), .b(xor_31_out), .out(in_3[30]), .cin(adder_30_cout), .cout(adder_31_cout));
  Adder #(.width(1)) adder_32 (.a(A[31]), .b(xor_32_out), .out(in_3[31]), .cin(adder_31_cout), .cout(out_5));
  not not_3 (not_3_out, in_3[31]);
  and and_1 (and_1_out, in_3[31], not_2_out, not_1_out);
  and and_2 (and_2_out, not_3_out, A[31], xor_32_out);
  or or_1 (out_6, and_1_out, and_2_out);

  // Notes on the sheet:
  //   4
  //   8
  //   12
  //   16
  //   20
  //   24
  //   28
  //   32
  //   4
  //   8
  //   12
  //   16
  //   24
  //   28
  //   32
  //   20
endmodule
