// Logisim project ALUControl.circ as structural Verilog: 1 circuit, main circuit main
module main (
  input  [5:0] Function,
  input  [2:0] ALUOp,
  output [3:0] ALUControlInput
);

  wire and_1_out, and_2_out, and_3_out, and_4_out, and_5_out, and_6_out, and_7_out, and_8_out, and_9_out,
       and_10_out, and_11_out, and_12_out, and_13_out, and_14_out, and_15_out, and_16_out, and_17_out,
       not_1_out, not_2_out, not_3_out, not_4_out, not_5_out, not_6_out, not_7_out, not_8_out;

  not not_1 (not_1_out, ALUOp[0]);
  not not_2 (not_2_out, ALUOp[1]);
  not not_3 (not_3_out, ALUOp[2]);
  not not_4 (not_4_out, Function[0]);
  not not_5 (not_5_out, Function[1]);
  not not_6 (not_6_out, Function[3]);
  not not_7 (not_7_out, Function[4]);
  not not_8 (not_8_out, Function[2]);
  and and_1 (and_1_out, Function[5], not_7_out, not_6_out, Function[2], not_5_out, not_4_out, not_3_out, not_2_out, not_1_out);
  and and_2 (and_2_out, Function[5], not_7_out, not_6_out, Function[2], Function[1], not_4_out, not_3_out, not_2_out, not_1_out);
  and and_3 (and_3_out, Function[5], not_7_out, not_6_out, not_8_out, Function[1], not_4_out, not_3_out, not_2_out, not_1_out);
  and and_4 (and_4_out, not_3_out, not_2_out, ALUOp[0]);
  and and_5 (and_5_out, not_3_out, ALUOp[1], ALUOp[0]);
  and and_6 (and_6_out, ALUOp[2], not_2_out, ALUOp[0]);
  and and_7 (and_7_out, Function[5], not_7_out, not_6_out, Function[2], not_5_out, Function[0], not_3_out, not_2_out, not_1_out);
  and and_8 (and_8_out, Function[5], not_7_out, not_6_out, Function[2], Function[1], not_4_out, not_3_out, not_2_out, not_1_out);
  and and_9 (and_9_out, Function[5], not_7_out, Function[3], not_8_out, Function[1], not_4_out, not_3_out, not_2_out, not_1_out);
  and and_10 (and_10_out, ALUOp[2], not_2_out, ALUOp[0]);
  and and_11 (and_11_out, not_3_out, ALUOp[1], not_1_out);
  and and_12 (and_12_out, not_3_out, ALUOp[1], ALUOp[0]);
  and and_13 (and_13_out, Function[5], not_7_out, not_6_out, not_8_out, not_5_out, not_4_out, not_3_out, not_2_out, not_1_out);
  and and_14 (and_14_out, Function[5], not_7_out, not_6_out, not_8_out, Function[1], not_4_out, not_3_out, not_2_out, not_1_out);
  and and_15 (and_15_out, Function[5], not_7_out, Function[3], not_8_out, Function[1], not_4_out, not_3_out, not_2_out, not_1_out);
  and and_16 (and_16_out, ALUOp[2], not_2_out, not_1_out);
  and and_17 (and_17_out, ALUOp[2], not_2_out, ALUOp[0]);
  or or_1 (ALUControlInput[0], and_1_out, and_2_out, and_3_out, and_4_out, and_5_out, and_6_out);
  or or_2 (ALUControlInput[1], and_7_out, and_8_out, and_9_out, and_10_out, and_11_out, and_12_out);
  or or_3 (ALUControlInput[2], and_13_out, and_14_out, and_15_out, and_16_out, and_17_out);

  assign ALUControlInput[3] = 1'b0;

  // Notes on the sheet:
  //   ALUControlBit3
endmodule
