// Logisim project AND.circ as structural Verilog: 1 circuit, main circuit main
module main (
  input  [31:0] in_1,
  input  [31:0] in_2,
  output [31:0] out_3
);

  and and_1 (out_3[31], in_1[31], in_2[31]);
  and and_2 (out_3[30], in_1[29], in_2[29]);
  and and_3 (out_3[28], in_1[28], in_2[28]);
  and and_4 (out_3[29], in_1[30], in_2[30]);
  and and_5 (out_3[27], in_1[27], in_2[27]);
  and and_6 (out_3[25], in_1[25], in_2[25]);
  and and_7 (out_3[24], in_2[24], in_1[24]);
  and and_8 (out_3[26], in_1[26], in_2[26]);
  and and_9 (out_3[23], in_1[23], in_2[23]);
  and and_10 (out_3[21], in_1[21], in_2[22]);
  and and_11 (out_3[20], in_2[20], in_1[20]);
  and and_12 (out_3[22], in_1[22], in_2[21]);
  and and_13 (out_3[19], in_1[19], in_2[19]);
  and and_14 (out_3[18], in_1[17], in_2[17]);
  and and_15 (out_3[16], in_2[16], in_1[16]);
  and and_16 (out_3[17], in_1[18], in_2[18]);
  and and_17 (out_3[15], in_1[15], in_2[15]);
  and and_18 (out_3[14], in_1[14], in_2[13]);
  and and_19 (out_3[12], in_1[12], in_2[12]);
  and and_20 (out_3[13], in_1[13], in_2[14]);
  and and_21 (out_3[11], in_1[11], in_2[11]);
  and and_22 (out_3[10], in_1[9], in_2[10]);
  and and_23 (out_3[9], in_1[8], in_2[8]);
  and and_24 (out_3[8], in_1[10], in_2[9]);
  and and_25 (out_3[7], in_1[7], in_2[7]);
  and and_26 (out_3[6], in_1[6], in_2[5]);
  and and_27 (out_3[5], in_1[4], in_2[4]);
  and and_28 (out_3[4], in_1[5], in_2[6]);
  and and_29 (out_3[3], in_1[3], in_2[3]);
  and and_30 (out_3[2], in_1[2], in_2[2]);
  and and_31 (out_3[1], in_1[0], in_2[0]);
  and and_32 (out_3[0], in_1[1], in_2[1]);

  // Notes on the sheet:
  //   A
  //   B
endmodule
