// Logisim project DataMemory.circ as structural Verilog: 1 circuit, main circuit main
module main (
  input  [31:0] in_1,
  input  MemWrite,
  input  Clock,
  input  MemRead,
  input  [31:0] in_5,
  output [31:0] Data_Read
);

  RAM #(.addrWidth(24), .dataWidth(32), .bus("separate")) ram_1 (
    .addr(in_1[23:0]), .din(in_5), .data(Data_Read), .str(MemWrite), .clk(Clock), .ld(MemRead));  // open: sel, clr

  // Notes on the sheet:
  //   Address
  //   Data
endmodule
