// Logisim project Datapath.circ as structural Verilog: 13 circuits, main circuit Datapath
module ALU (
  input  [1:0] Shift_Operation,
  input  [31:0] Bus_A,
  input  [31:0] Bus_B,
  input  [3:0] ALU_Control,
  output [31:0] ALU_Result,
  output Zero
);

  wire adder_1_cout, comparator_1_lt, multiplexer_3_out, not_5_out;
  wire [1:0] demultiplexer_1_out6, multiplexer_1_out, multiplexer_4_out, not_1_out, not_3_out, not_6_out,
       not_7_out;
  wire [1:1] demultiplexer_1_out1, demultiplexer_1_out3;
  wire [31:0] adder_1_out, and_1_out, bit_extender_1_out, multiplexer_2_out, not_4_out, or_1_out,
       shifter_1_out_4, xor_1_out, xor_gate_1_output;

  Demultiplexer #(.select(4)) demultiplexer_1 (
    .out1(demultiplexer_1_out1[1]), .out2(not_3_out[0]), .out3(demultiplexer_1_out3[1]), .out4(not_6_out[1]),
    .out5(not_7_out[1]), .out6(demultiplexer_1_out6[0]), .in(1'b1), .sel(ALU_Control));  // open: out0, out7, out8, out9, out10, out11, out12, out13, out14, out15, en
  not not_1 (not_1_out[0], demultiplexer_1_out1[1]);
  not not_2 (not_1_out[1], demultiplexer_1_out1[1]);
  assign and_1_out = Bus_A & Bus_B;  // AND_Gate and_1, 32 bits wide
  assign or_1_out = Bus_A | Bus_B;  // OR_Gate or_1, 32 bits wide
  assign xor_1_out = Bus_A ^ Bus_B;  // XOR_Gate xor_1, 32 bits wide
  Multiplexer #(.select(4), .width(2)) multiplexer_1 (
    .in1(not_1_out), .in2(not_3_out), .in3({2{demultiplexer_1_out3[1]}}), .out(multiplexer_1_out),
    .sel(ALU_Control));  // open: in0, in4, in5, in6, in7, in8, in9, in10, in11, in12, in13, in14, in15, en
  not not_3 (not_3_out[1], not_3_out[0]);
  shifter shifter_1 (.ShiftAmt(Bus_A[4:0]), .Input(Bus_A), .ShifterControl(Shift_Operation), .out_4(shifter_1_out_4));
  xor_gate xor_gate_1 (.BusB(Bus_B), .Control_Input(multiplexer_3_out), .Output(xor_gate_1_output));
  Multiplexer #(.select(2), .width(32)) multiplexer_2 (
    .in0(and_1_out), .in1(or_1_out), .in2(not_4_out), .in3(xor_1_out), .out(multiplexer_2_out),
    .sel(multiplexer_1_out));  // open: en
  assign not_4_out = ~or_1_out;  // NOT_Gate not_4, 32 bits wide
  Multiplexer #(.select(4)) multiplexer_3 (
    .in4(not_5_out), .in5(not_7_out[1]), .in6(demultiplexer_1_out6[0]), .out(multiplexer_3_out),
    .sel(ALU_Control));  // open: in0, in1, in2, in3, in7, in8, in9, in10, in11, in12, in13, in14, in15, en
  not not_5 (not_5_out, not_6_out[1]);
  Comparator #(.width(1)) comparator_1 (.a(adder_1_out[31]), .b(adder_1_cout), .lt(comparator_1_lt));  // open: gt, eq
  Adder #(.width(32)) adder_1 (
    .a(Bus_A), .b(xor_gate_1_output), .out(adder_1_out), .cin(multiplexer_3_out), .cout(adder_1_cout));
  Multiplexer #(.select(4), .width(2)) multiplexer_4 (
    .in1({2{demultiplexer_1_out1[1]}}), .in2({2{not_3_out[0]}}), .in3({2{demultiplexer_1_out3[1]}}),
    .in4(not_6_out), .in5(not_7_out), .in6(demultiplexer_1_out6), .out(multiplexer_4_out), .sel(ALU_Control));  // open: in0, in7, in8, in9, in10, in11, in12, in13, in14, in15, en
  not not_6 (not_6_out[0], not_6_out[1]);
  assign bit_extender_1_out = {{31{1'b0}}, comparator_1_lt};  // Bit_Extender bit_extender_1
  not not_7 (not_7_out[0], not_7_out[1]);
  not not_8 (demultiplexer_1_out6[1], demultiplexer_1_out6[0]);
  Multiplexer #(.select(2), .width(32)) multiplexer_5 (
    .in0(shifter_1_out_4), .in1(bit_extender_1_out), .in2(adder_1_out), .in3(multiplexer_2_out),
    .out(ALU_Result), .sel(multiplexer_4_out));  // open: en
  nor nor_1 (Zero, ALU_Result[31], ALU_Result[30], ALU_Result[29], ALU_Result[28], ALU_Result[27], ALU_Result[26], ALU_Result[25], ALU_Result[24], ALU_Result[23], ALU_Result[22], ALU_Result[21], ALU_Result[20], ALU_Result[19], ALU_Result[18], ALU_Result[17], ALU_Result[16], ALU_Result[15], ALU_Result[14], ALU_Result[13], ALU_Result[12], ALU_Result[11], ALU_Result[10], ALU_Result[9], ALU_Result[8], ALU_Result[7], ALU_Result[6], ALU_Result[5], ALU_Result[4], ALU_Result[3], ALU_Result[2], ALU_Result[1], ALU_Result[0]);
endmodule

module shifter (
  input  [4:0] ShiftAmt,
  input  [31:0] Input,
  input  [1:0] ShifterControl,
  output [31:0] out_4
);

  wire [31:0] shifter_1_out, shifter_2_out, shifter_3_out;

  Shifter #(.width(32)) shifter_1 (.in(Input), .\dist (ShiftAmt), .out(shifter_1_out));
  Shifter #(.width(32), .shift("lr")) shifter_2 (.in(Input), .\dist (ShiftAmt), .out(shifter_2_out));
  Shifter #(.width(32), .shift("ar")) shifter_3 (.in(Input), .\dist (ShiftAmt), .out(shifter_3_out));
  Multiplexer #(.select(2), .width(32)) multiplexer_1 (
    .in1(shifter_1_out), .in2(shifter_2_out), .in3(shifter_3_out), .out(out_4), .sel(ShifterControl));  // open: in0, en
endmodule

module xor_gate (
  input  [31:0] BusB,
  input  Control_Input,
  output [31:0] Output
);

  xor xor_1 (Output[0], BusB[0], Control_Input);
  xor xor_2 (Output[1], BusB[1], Control_Input);
  xor xor_3 (Output[2], BusB[2], Control_Input);
  xor xor_4 (Output[3], BusB[3], Control_Input);
  xor xor_5 (Output[4], BusB[4], Control_Input);
  xor xor_6 (Output[5], BusB[5], Control_Input);
  xor xor_7 (Output[6], BusB[6], Control_Input);
  xor xor_8 (Output[7], BusB[7], Control_Input);
  xor xor_9 (Output[8], BusB[8], Control_Input);
  xor xor_10 (Output[9], BusB[9], Control_Input);
  xor xor_11 (Output[10], BusB[10], Control_Input);
  xor xor_12 (Output[11], BusB[11], Control_Input);
  xor xor_13 (Output[12], BusB[12], Control_Input);
  xor xor_14 (Output[13], BusB[13], Control_Input);
  xor xor_15 (Output[14], BusB[14], Control_Input);
  xor xor_16 (Output[15], BusB[15], Control_Input);
  xor xor_17 (Output[16], BusB[16], Control_Input);
  xor xor_18 (Output[17], BusB[17], Control_Input);
  xor xor_19 (Output[18], BusB[18], Control_Input);
  xor xor_20 (Output[19], BusB[19], Control_Input);
  xor xor_21 (Output[20], BusB[20], Control_Input);
  xor xor_22 (Output[21], BusB[21], Control_Input);
  xor xor_23 (Output[22], BusB[22], Control_Input);
  xor xor_24 (Output[23], BusB[23], Control_Input);
  xor xor_25 (Output[24], BusB[24], Control_Input);
  xor xor_26 (Output[25], BusB[25], Control_Input);
  xor xor_27 (Output[26], BusB[26], Control_Input);
  xor xor_28 (Output[27], BusB[27], Control_Input);
  xor xor_29 (Output[28], BusB[28], Control_Input);
  xor xor_30 (Output[29], BusB[29], Control_Input);
  xor xor_31 (Output[30], BusB[30], Control_Input);
  xor xor_32 (Output[31], BusB[31], Control_Input);

  // Notes on the sheet:
  //   1
  //   5
  //   10
  //   15
  //   20
  //   25
endmodule

module Datapath (
);

  wire alu_1_zero, clock_1_out, Main_Control_alusrc, Main_Control_beq, Main_Control_bne, Main_Control_extop,
       Main_Control_jump, Main_Control_memrd, Main_Control_memtoreg, Main_Control_memwr, Main_Control_regdst,
       Main_Control_regwrite;
  wire [1:0] PC_Control_select_bits;
  wire [3:0] adder_1_out_2, ALU_Control_alu_control;
  wire [4:0] Instruction_Memory_rd, Instruction_Memory_rs, Instruction_Memory_rt, multiplexer_2_out;
  wire [5:0] Instruction_Memory_function, Instruction_Memory_opcode;
  wire [15:0] Instruction_Memory__16_immediate;
  wire [25:0] Instruction_Memory__26_bit_immediate;
  wire [27:0] adder_1_out;
  wire [31:0] adder_2_out, alu_1_alu_result, Data_Memory_data_output, Extender__32_bit_output,
       multiplexer_1_out, multiplexer_3_out, multiplexer_4_out, Program_Count_q, Register_FIle_busa,
       Register_FIle_busb;

  Multiplexer #(.select(2), .width(32)) multiplexer_1 (
    .in0({adder_1_out_2, adder_1_out}), .in1({adder_1_out_2, Instruction_Memory__26_bit_immediate, 2'b00}),
    .in2(adder_2_out), .out(multiplexer_1_out), .sel(PC_Control_select_bits));  // open: in3, en
  PC_Control PC_Control (
    .Select_Bits(PC_Control_select_bits), .BNE(Main_Control_bne), .BEQ(Main_Control_beq),
    .Jump(Main_Control_jump), .Zero(alu_1_zero));
  Register #(.width(32)) Program_Count (
    .D(multiplexer_1_out), .Q(Program_Count_q), .clk(clock_1_out));  // open: en, clr
  Clock clock_1 (.out(clock_1_out));
  Adder #(.width(32)) adder_1 (.a(32'h4), .b(Program_Count_q), .out({adder_1_out_2, adder_1_out}));  // open: cin, cout
  instructionMemory Instruction_Memory (
    .PC_Address(Program_Count_q), .Clock(clock_1_out), .Load_Enabler(1'b1),
    .opcode(Instruction_Memory_opcode), .rs(Instruction_Memory_rs), .rt(Instruction_Memory_rt),
    .rd(Instruction_Memory_rd), .\function (Instruction_Memory_function),
    ._16_Immediate(Instruction_Memory__16_immediate), ._26_Bit_Immediate(Instruction_Memory__26_bit_immediate));  // open: shift_amount
  Main_Control Main_Control (
    .BEQ(Main_Control_beq), .BNE(Main_Control_bne), .Jump(Main_Control_jump), .RegDst(Main_Control_regdst),
    .RegWrite(Main_Control_regwrite), .ExtOp(Main_Control_extop), .ALUSrc(Main_Control_alusrc),
    .MemRd(Main_Control_memrd), .MemWr(Main_Control_memwr), .MemtoReg(Main_Control_memtoreg),
    .opcode(Instruction_Memory_opcode));
  Extender Extender (
    ._16_Bit_Input(Instruction_Memory__16_immediate), .ExtOp(Main_Control_extop),
    ._32_Bit_Output(Extender__32_bit_output));
  Multiplexer #(.width(5)) multiplexer_2 (
    .in0(Instruction_Memory_rt), .in1(Instruction_Memory_rd), .out(multiplexer_2_out),
    .sel(Main_Control_regdst));  // open: en
  Adder #(.width(32)) adder_2 (
    .a({adder_1_out_2, adder_1_out}), .b(Extender__32_bit_output), .out(adder_2_out));  // open: cin, cout
  registerFile Register_FIle (
    .RA(Instruction_Memory_rs), .RB(Instruction_Memory_rt), .RW(multiplexer_2_out),
    .RegWrite(Main_Control_regwrite), .BusW(multiplexer_4_out), .busA(Register_FIle_busa),
    .busB(Register_FIle_busb));
  Multiplexer #(.width(32)) multiplexer_3 (
    .in0(Extender__32_bit_output), .in1(Register_FIle_busb), .out(multiplexer_3_out),
    .sel(Main_Control_alusrc));  // open: en
  ALU_Control ALU_Control (
    .opcode(Instruction_Memory_opcode), .\function (Instruction_Memory_function),
    .ALU_Control(ALU_Control_alu_control));
  ALU alu_1 (
    .Bus_A(Register_FIle_busa), .Bus_B(multiplexer_3_out), .ALU_Control(ALU_Control_alu_control),
    .Zero(alu_1_zero), .ALU_Result(alu_1_alu_result));  // open: Shift_Operation
  Data_Memory Data_Memory (
    .Address(alu_1_alu_result), .MemWrite(Main_Control_memwr), .Clock(clock_1_out),
    .Data_Input(Register_FIle_busb), .MemRead(Main_Control_memrd), .Data_Output(Data_Memory_data_output));
  Multiplexer #(.width(32)) multiplexer_4 (
    .in0(alu_1_alu_result), .in1(Data_Memory_data_output), .out(multiplexer_4_out),
    .sel(Main_Control_memtoreg));  // open: en
  Multiplexer #(.width(32)) multiplexer_5 ();  // open: in0, in1, out, sel, en
endmodule

module registerFile (
  input  RegWrite,
  input  [31:0] BusW,
  input  [4:0] RA,
  input  [4:0] RB,
  input  [4:0] RW,
  output [31:0] busA,
  output [31:0] busB
);

  wire and_1_out, and_2_out, and_3_out, and_4_out, and_5_out, and_6_out, and_7_out, and_8_out, and_9_out,
       and_10_out, and_11_out, and_12_out, and_13_out, and_14_out, and_15_out, and_16_out, and_17_out,
       and_18_out, and_19_out, and_20_out, and_21_out, and_22_out, and_23_out, and_24_out, and_25_out,
       and_26_out, and_27_out, and_28_out, and_29_out, and_30_out, and_31_out, clock_1_out, decoder_1_out1,
       decoder_1_out2, decoder_1_out3, decoder_1_out4, decoder_1_out5, decoder_1_out6, decoder_1_out7,
       decoder_1_out8, decoder_1_out9, decoder_1_out10, decoder_1_out11, decoder_1_out12, decoder_1_out13,
       decoder_1_out14, decoder_1_out15, decoder_1_out16, decoder_1_out17, decoder_1_out18, decoder_1_out19,
       decoder_1_out20, decoder_1_out21, decoder_1_out22, decoder_1_out23, decoder_1_out24, decoder_1_out25,
       decoder_1_out26, decoder_1_out27, decoder_1_out28, decoder_1_out29, decoder_1_out30, decoder_1_out31,
       decoder_2_out0, decoder_2_out1, decoder_2_out2, decoder_2_out3, decoder_2_out4, decoder_2_out5,
       decoder_2_out6, decoder_2_out7, decoder_2_out8, decoder_2_out9, decoder_2_out10, decoder_2_out11,
       decoder_2_out12, decoder_2_out13, decoder_2_out14, decoder_2_out15, decoder_2_out16, decoder_2_out17,
       decoder_2_out18, decoder_2_out19, decoder_2_out20, decoder_2_out21, decoder_2_out22, decoder_2_out23,
       decoder_2_out24, decoder_2_out25, decoder_2_out26, decoder_2_out27, decoder_2_out28, decoder_2_out29,
       decoder_2_out30, decoder_2_out31, decoder_3_out0, decoder_3_out1, decoder_3_out2, decoder_3_out3,
       decoder_3_out4, decoder_3_out5, decoder_3_out6, decoder_3_out7, decoder_3_out8, decoder_3_out9,
       decoder_3_out10, decoder_3_out11, decoder_3_out12, decoder_3_out13, decoder_3_out14, decoder_3_out15,
       decoder_3_out16, decoder_3_out17, decoder_3_out18, decoder_3_out19, decoder_3_out20, decoder_3_out21,
       decoder_3_out22, decoder_3_out23, decoder_3_out24, decoder_3_out25, decoder_3_out26, decoder_3_out27,
       decoder_3_out28, decoder_3_out29, decoder_3_out30, decoder_3_out31;
  wire [31:0] R0_q, R1_q, R2_q, R3_q, R4_q, R5_q, R6_q, R7_q, R8_q, R9_q, R10_q, R11_q, R12_q, R13_q, R14_q,
       R15_q, R16_q, R17_q, R18_q, R19_q, R20_q, R21_q, R22_q, R23_q, R24_q, R25_q, R26_q, R27_q, R28_q,
       R30_q, R31_q;

  Decoder #(.select(5)) decoder_1 (
    .out1(decoder_1_out1), .out2(decoder_1_out2), .out3(decoder_1_out3), .out4(decoder_1_out4),
    .out5(decoder_1_out5), .out6(decoder_1_out6), .out7(decoder_1_out7), .out8(decoder_1_out8),
    .out9(decoder_1_out9), .out10(decoder_1_out10), .out11(decoder_1_out11), .out12(decoder_1_out12),
    .out13(decoder_1_out13), .out14(decoder_1_out14), .out15(decoder_1_out15), .out16(decoder_1_out16),
    .out17(decoder_1_out17), .out18(decoder_1_out18), .out19(decoder_1_out19), .out20(decoder_1_out20),
    .out21(decoder_1_out21), .out22(decoder_1_out22), .out23(decoder_1_out23), .out24(decoder_1_out24),
    .out25(decoder_1_out25), .out26(decoder_1_out26), .out27(decoder_1_out27), .out28(decoder_1_out28),
    .out29(decoder_1_out29), .out30(decoder_1_out30), .out31(decoder_1_out31), .sel(RW));  // open: out0, en
  Decoder #(.select(5)) decoder_2 (
    .out0(decoder_2_out0), .out1(decoder_2_out1), .out2(decoder_2_out2), .out3(decoder_2_out3),
    .out4(decoder_2_out4), .out5(decoder_2_out5), .out6(decoder_2_out6), .out7(decoder_2_out7),
    .out8(decoder_2_out8), .out9(decoder_2_out9), .out10(decoder_2_out10), .out11(decoder_2_out11),
    .out12(decoder_2_out12), .out13(decoder_2_out13), .out14(decoder_2_out14), .out15(decoder_2_out15),
    .out16(decoder_2_out16), .out17(decoder_2_out17), .out18(decoder_2_out18), .out19(decoder_2_out19),
    .out20(decoder_2_out20), .out21(decoder_2_out21), .out22(decoder_2_out22), .out23(decoder_2_out23),
    .out24(decoder_2_out24), .out25(decoder_2_out25), .out26(decoder_2_out26), .out27(decoder_2_out27),
    .out28(decoder_2_out28), .out29(decoder_2_out29), .out30(decoder_2_out30), .out31(decoder_2_out31),
    .sel(RA), .en(1'b1));
  Decoder #(.select(5)) decoder_3 (
    .out0(decoder_3_out0), .out1(decoder_3_out1), .out2(decoder_3_out2), .out3(decoder_3_out3),
    .out4(decoder_3_out4), .out5(decoder_3_out5), .out6(decoder_3_out6), .out7(decoder_3_out7),
    .out8(decoder_3_out8), .out9(decoder_3_out9), .out10(decoder_3_out10), .out11(decoder_3_out11),
    .out12(decoder_3_out12), .out13(decoder_3_out13), .out14(decoder_3_out14), .out15(decoder_3_out15),
    .out16(decoder_3_out16), .out17(decoder_3_out17), .out18(decoder_3_out18), .out19(decoder_3_out19),
    .out20(decoder_3_out20), .out21(decoder_3_out21), .out22(decoder_3_out22), .out23(decoder_3_out23),
    .out24(decoder_3_out24), .out25(decoder_3_out25), .out26(decoder_3_out26), .out27(decoder_3_out27),
    .out28(decoder_3_out28), .out29(decoder_3_out29), .out30(decoder_3_out30), .out31(decoder_3_out31),
    .sel(RB), .en(1'b1));
  and and_1 (and_1_out, RegWrite, decoder_1_out1);
  and and_2 (and_2_out, RegWrite, decoder_1_out3);
  and and_3 (and_3_out, RegWrite, decoder_1_out5);
  and and_4 (and_4_out, RegWrite, decoder_1_out7);
  and and_5 (and_5_out, RegWrite, decoder_1_out9);
  and and_6 (and_6_out, RegWrite, decoder_1_out11);
  and and_7 (and_7_out, RegWrite, decoder_1_out13);
  and and_8 (and_8_out, RegWrite, decoder_1_out15);
  and and_9 (and_9_out, RegWrite, decoder_1_out17);
  and and_10 (and_10_out, RegWrite, decoder_1_out19);
  and and_11 (and_11_out, RegWrite, decoder_1_out21);
  and and_12 (and_12_out, RegWrite, decoder_1_out23);
  and and_13 (and_13_out, RegWrite, decoder_1_out25);
  and and_14 (and_14_out, RegWrite, decoder_1_out27);
  and and_15 (and_15_out, RegWrite, decoder_1_out29);
  and and_16 (and_16_out, RegWrite, decoder_1_out31);
  assign busA = decoder_2_out0 ? R0_q : 32'bz;  // Controlled_Buffer controlled_buffer_1
  and and_17 (and_17_out, RegWrite, decoder_1_out2);
  and and_18 (and_18_out, RegWrite, decoder_1_out4);
  and and_19 (and_19_out, RegWrite, decoder_1_out6);
  and and_20 (and_20_out, RegWrite, decoder_1_out8);
  and and_21 (and_21_out, RegWrite, decoder_1_out10);
  and and_22 (and_22_out, RegWrite, decoder_1_out12);
  and and_23 (and_23_out, RegWrite, decoder_1_out14);
  and and_24 (and_24_out, RegWrite, decoder_1_out16);
  and and_25 (and_25_out, RegWrite, decoder_1_out18);
  and and_26 (and_26_out, RegWrite, decoder_1_out20);
  and and_27 (and_27_out, RegWrite, decoder_1_out22);
  and and_28 (and_28_out, RegWrite, decoder_1_out24);
  and and_29 (and_29_out, RegWrite, decoder_1_out26);
  and and_30 (and_30_out, RegWrite, decoder_1_out28);
  and and_31 (and_31_out, RegWrite, decoder_1_out30);
  assign busB = decoder_3_out0 ? R0_q : 32'bz;  // Controlled_Buffer controlled_buffer_2
  Clock clock_1 (.out(clock_1_out));
  Register #(.width(32)) R1 (.D(BusW), .en(and_1_out), .Q(R1_q), .clk(clock_1_out), .clr(1'b0));
  Register #(.width(32)) R2 (.D(BusW), .en(and_17_out), .Q(R2_q), .clk(clock_1_out), .clr(1'b0));
  Register #(.width(32)) R3 (.D(BusW), .en(and_2_out), .Q(R3_q), .clk(clock_1_out), .clr(1'b0));
  Register #(.width(32)) R4 (.D(BusW), .en(and_18_out), .Q(R4_q), .clk(clock_1_out), .clr(1'b0));
  Register #(.width(32)) R5 (.D(BusW), .en(and_3_out), .Q(R5_q), .clk(clock_1_out), .clr(1'b0));
  Register #(.width(32)) R6 (.D(BusW), .en(and_19_out), .Q(R6_q), .clk(clock_1_out), .clr(1'b0));
  Register #(.width(32)) R7 (.D(BusW), .en(and_4_out), .Q(R7_q), .clk(clock_1_out), .clr(1'b0));
  Register #(.width(32)) R8 (.D(BusW), .en(and_20_out), .Q(R8_q), .clk(clock_1_out), .clr(1'b0));
  Register #(.width(32)) R9 (.D(BusW), .en(and_5_out), .Q(R9_q), .clk(clock_1_out), .clr(1'b0));
  Register #(.width(32)) R10 (.D(BusW), .en(and_21_out), .Q(R10_q), .clk(clock_1_out), .clr(1'b0));
  Register #(.width(32)) R11 (.D(BusW), .en(and_6_out), .Q(R11_q), .clk(clock_1_out), .clr(1'b0));
  Register #(.width(32)) R12 (.D(BusW), .en(and_22_out), .Q(R12_q), .clk(clock_1_out), .clr(1'b0));
  Register #(.width(32)) R13 (.D(BusW), .en(and_7_out), .Q(R13_q), .clk(clock_1_out), .clr(1'b0));
  Register #(.width(32)) R14 (.D(BusW), .en(and_23_out), .Q(R14_q), .clk(clock_1_out), .clr(1'b0));
  Register #(.width(32)) R15 (.D(BusW), .en(and_8_out), .Q(R15_q), .clk(clock_1_out), .clr(1'b0));
  Register #(.width(32)) R16 (.D(BusW), .en(and_24_out), .Q(R16_q), .clk(clock_1_out), .clr(1'b0));
  Register #(.width(32)) R17 (.D(BusW), .en(and_9_out), .Q(R17_q), .clk(clock_1_out), .clr(1'b0));
  Register #(.width(32)) R0 (.Q(R0_q), .clk(clock_1_out));  // open: D, en, clr
  Register #(.width(32)) R18 (.D(BusW), .en(and_25_out), .Q(R18_q), .clk(clock_1_out), .clr(1'b0));
  Register #(.width(32)) R19 (.D(BusW), .en(and_10_out), .Q(R19_q), .clk(clock_1_out), .clr(1'b0));
  Register #(.width(32)) R20 (.D(BusW), .en(and_26_out), .Q(R20_q), .clk(clock_1_out), .clr(1'b0));
  Register #(.width(32)) R21 (.D(BusW), .en(and_11_out), .Q(R21_q), .clk(clock_1_out), .clr(1'b0));
  Register #(.width(32)) R22 (.D(BusW), .en(and_27_out), .Q(R22_q), .clk(clock_1_out), .clr(1'b0));
  Register #(.width(32)) R23 (.D(BusW), .en(and_12_out), .Q(R23_q), .clk(clock_1_out), .clr(1'b0));
  Register #(.width(32)) R24 (.D(BusW), .en(and_28_out), .Q(R24_q), .clk(clock_1_out), .clr(1'b0));
  Register #(.width(32)) R25 (.D(BusW), .en(and_13_out), .Q(R25_q), .clk(clock_1_out), .clr(1'b0));
  Register #(.width(32)) R26 (.D(BusW), .en(and_29_out), .Q(R26_q), .clk(clock_1_out), .clr(1'b0));
  Register #(.width(32)) R27 (.D(BusW), .en(and_14_out), .Q(R27_q), .clk(clock_1_out), .clr(1'b0));
  Register #(.width(32)) R28 (.D(BusW), .en(and_30_out), .Q(R28_q), .clk(clock_1_out), .clr(1'b0));
  Register #(.width(32)) R29 (.D(BusW), .en(and_15_out), .Q(R17_q), .clk(clock_1_out), .clr(1'b0));
  Register #(.width(32)) R30 (.D(BusW), .en(and_31_out), .Q(R30_q), .clk(clock_1_out), .clr(1'b0));
  Register #(.width(32)) R31 (.D(BusW), .en(and_16_out), .Q(R31_q), .clk(clock_1_out), .clr(1'b0));
  assign busA = decoder_2_out31 ? R31_q : 32'bz;  // Controlled_Buffer controlled_buffer_3
  assign busB = decoder_3_out31 ? R31_q : 32'bz;  // Controlled_Buffer controlled_buffer_4
  assign busA = decoder_2_out30 ? R30_q : 32'bz;  // Controlled_Buffer controlled_buffer_5
  assign busA = decoder_2_out29 ? R17_q : 32'bz;  // Controlled_Buffer controlled_buffer_6
  assign busB = decoder_3_out30 ? R30_q : 32'bz;  // Controlled_Buffer controlled_buffer_7
  assign busB = decoder_3_out29 ? R17_q : 32'bz;  // Controlled_Buffer controlled_buffer_8
  assign busA = decoder_2_out28 ? R28_q : 32'bz;  // Controlled_Buffer controlled_buffer_9
  assign busB = decoder_3_out28 ? R28_q : 32'bz;  // Controlled_Buffer controlled_buffer_10
  assign busA = decoder_2_out27 ? R27_q : 32'bz;  // Controlled_Buffer controlled_buffer_11
  assign busB = decoder_3_out27 ? R27_q : 32'bz;  // Controlled_Buffer controlled_buffer_12
  assign busB = decoder_3_out26 ? R26_q : 32'bz;  // Controlled_Buffer controlled_buffer_13
  assign busA = decoder_2_out26 ? R26_q : 32'bz;  // Controlled_Buffer controlled_buffer_14
  assign busA = decoder_2_out25 ? R25_q : 32'bz;  // Controlled_Buffer controlled_buffer_15
  assign busB = decoder_3_out25 ? R25_q : 32'bz;  // Controlled_Buffer controlled_buffer_16
  assign busA = decoder_2_out24 ? R24_q : 32'bz;  // Controlled_Buffer controlled_buffer_17
  assign busB = decoder_3_out24 ? R24_q : 32'bz;  // Controlled_Buffer controlled_buffer_18
  assign busA = decoder_2_out23 ? R23_q : 32'bz;  // Controlled_Buffer controlled_buffer_19
  assign busA = decoder_2_out22 ? R22_q : 32'bz;  // Controlled_Buffer controlled_buffer_20
  assign busB = decoder_3_out23 ? R23_q : 32'bz;  // Controlled_Buffer controlled_buffer_21
  assign busB = decoder_3_out22 ? R22_q : 32'bz;  // Controlled_Buffer controlled_buffer_22
  assign busA = decoder_2_out21 ? R21_q : 32'bz;  // Controlled_Buffer controlled_buffer_23
  assign busB = decoder_3_out21 ? R21_q : 32'bz;  // Controlled_Buffer controlled_buffer_24
  assign busA = decoder_2_out20 ? R20_q : 32'bz;  // Controlled_Buffer controlled_buffer_25
  assign busB = decoder_3_out20 ? R20_q : 32'bz;  // Controlled_Buffer controlled_buffer_26
  assign busA = decoder_2_out19 ? R19_q : 32'bz;  // Controlled_Buffer controlled_buffer_27
  assign busB = decoder_3_out19 ? R19_q : 32'bz;  // Controlled_Buffer controlled_buffer_28
  assign busA = decoder_2_out18 ? R18_q : 32'bz;  // Controlled_Buffer controlled_buffer_29
  assign busB = decoder_3_out18 ? R18_q : 32'bz;  // Controlled_Buffer controlled_buffer_30
  assign busA = decoder_2_out17 ? R17_q : 32'bz;  // Controlled_Buffer controlled_buffer_31
  assign busB = decoder_3_out17 ? R17_q : 32'bz;  // Controlled_Buffer controlled_buffer_32
  assign busB = decoder_3_out16 ? R16_q : 32'bz;  // Controlled_Buffer controlled_buffer_33
  assign busA = decoder_2_out16 ? R16_q : 32'bz;  // Controlled_Buffer controlled_buffer_34
  assign busA = decoder_2_out15 ? R15_q : 32'bz;  // Controlled_Buffer controlled_buffer_35
  assign busB = decoder_3_out15 ? R15_q : 32'bz;  // Controlled_Buffer controlled_buffer_36
  assign busA = decoder_2_out14 ? R14_q : 32'bz;  // Controlled_Buffer controlled_buffer_37
  assign busB = decoder_3_out14 ? R14_q : 32'bz;  // Controlled_Buffer controlled_buffer_38
  assign busB = decoder_3_out13 ? R13_q : 32'bz;  // Controlled_Buffer controlled_buffer_39
  assign busA = decoder_2_out13 ? R13_q : 32'bz;  // Controlled_Buffer controlled_buffer_40
  assign busA = decoder_2_out12 ? R12_q : 32'bz;  // Controlled_Buffer controlled_buffer_41
  assign busA = decoder_2_out11 ? R11_q : 32'bz;  // Controlled_Buffer controlled_buffer_42
  assign busB = decoder_3_out12 ? R12_q : 32'bz;  // Controlled_Buffer controlled_buffer_43
  assign busB = decoder_3_out11 ? R11_q : 32'bz;  // Controlled_Buffer controlled_buffer_44
  assign busA = decoder_2_out10 ? R10_q : 32'bz;  // Controlled_Buffer controlled_buffer_45
  assign busA = decoder_2_out9 ? R9_q : 32'bz;  // Controlled_Buffer controlled_buffer_46
  assign busB = decoder_3_out10 ? R10_q : 32'bz;  // Controlled_Buffer controlled_buffer_47
  assign busB = decoder_3_out9 ? R9_q : 32'bz;  // Controlled_Buffer controlled_buffer_48
  assign busA = decoder_2_out8 ? R8_q : 32'bz;  // Controlled_Buffer controlled_buffer_49
  assign busB = decoder_3_out8 ? R8_q : 32'bz;  // Controlled_Buffer controlled_buffer_50
  assign busA = decoder_2_out7 ? R7_q : 32'bz;  // Controlled_Buffer controlled_buffer_51
  assign busB = decoder_3_out7 ? R7_q : 32'bz;  // Controlled_Buffer controlled_buffer_52
  assign busA = decoder_2_out6 ? R6_q : 32'bz;  // Controlled_Buffer controlled_buffer_53
  assign busA = decoder_2_out5 ? R5_q : 32'bz;  // Controlled_Buffer controlled_buffer_54
  assign busB = decoder_3_out6 ? R6_q : 32'bz;  // Controlled_Buffer controlled_buffer_55
  assign busB = decoder_3_out5 ? R5_q : 32'bz;  // Controlled_Buffer controlled_buffer_56
  assign busA = decoder_2_out4 ? R4_q : 32'bz;  // Controlled_Buffer controlled_buffer_57
  assign busB = decoder_3_out4 ? R4_q : 32'bz;  // Controlled_Buffer controlled_buffer_58
  assign busA = decoder_2_out3 ? R3_q : 32'bz;  // Controlled_Buffer controlled_buffer_59
  assign busB = decoder_3_out3 ? R3_q : 32'bz;  // Controlled_Buffer controlled_buffer_60
  assign busA = decoder_2_out2 ? R2_q : 32'bz;  // Controlled_Buffer controlled_buffer_61
  assign busB = decoder_3_out2 ? R2_q : 32'bz;  // Controlled_Buffer controlled_buffer_62
  assign busA = decoder_2_out1 ? R1_q : 32'bz;  // Controlled_Buffer controlled_buffer_63
  assign busB = decoder_3_out1 ? R1_q : 32'bz;  // Controlled_Buffer controlled_buffer_64
endmodule

module instructionMemory (
  input  [31:0] PC_Address,
  input  Clock,
  input  Load_Enabler,
  output [5:0] opcode,
  output [4:0] rs,
  output [4:0] rt,
  output [4:0] rd,
  output [4:0] shift_amount,
  output [5:0] \function ,
  output [15:0] _16_Immediate,
  output [25:0] _26_Bit_Immediate
);

  RAM #(.addrWidth(24), .dataWidth(32)) ram_1 (
    .addr(PC_Address[23:0]),
    .data({_16_Immediate, _26_Bit_Immediate[20:16], _26_Bit_Immediate[25:21], opcode}), .clk(Clock),
    .ld(Load_Enabler));  // open: sel, clr

  assign _26_Bit_Immediate[15:0] = _16_Immediate;
  assign \function  = _16_Immediate[15:10];
  assign rd = _16_Immediate[4:0];
  assign rs = _26_Bit_Immediate[25:21];
  assign rt = _26_Bit_Immediate[20:16];
  assign shift_amount = _16_Immediate[9:5];
endmodule

module Extender (
  input  [15:0] _16_Bit_Input,
  input  ExtOp,
  output [31:0] _32_Bit_Output
);

  wire [15:0] demultiplexer_1_out0, demultiplexer_1_out1;
  wire [31:0] bit_extender_1_out, bit_extender_2_out;

  Demultiplexer #(.width(16)) demultiplexer_1 (
    .out0(demultiplexer_1_out0), .out1(demultiplexer_1_out1), .in(_16_Bit_Input), .sel(ExtOp));  // open: en
  assign bit_extender_1_out = {{16{1'b0}}, demultiplexer_1_out0};  // Bit_Extender bit_extender_1
  assign bit_extender_2_out = {{16{demultiplexer_1_out1[15]}}, demultiplexer_1_out1};  // Bit_Extender bit_extender_2
  Multiplexer #(.width(32)) multiplexer_1 (
    .in0(bit_extender_1_out), .in1(bit_extender_2_out), .out(_32_Bit_Output), .sel(ExtOp));  // open: en
endmodule

module Main_Control (
  input  [5:0] opcode,
  output BEQ,
  output BNE,
  output Jump,
  output RegDst,
  output RegWrite,
  output ExtOp,
  output ALUSrc,
  output MemRd,
  output MemWr,
  output MemtoReg
);

  wire demultiplexer_2_out0, demultiplexer_2_out8, demultiplexer_2_out10, demultiplexer_2_out12,
       demultiplexer_2_out13, demultiplexer_2_out14, demultiplexer_3_out3, demultiplexer_3_out11, not_1_out,
       not_2_out, not_3_out, not_4_out, not_5_out, not_6_out, not_7_out, not_8_out, not_9_out, not_10_out,
       not_11_out, not_12_out, not_13_out, not_14_out, not_15_out, not_16_out, not_17_out, not_18_out,
       not_19_out, not_20_out, not_21_out, not_22_out, not_23_out, not_24_out, not_25_out, not_26_out,
       not_27_out, not_28_out, not_29_out, not_30_out, not_31_out, not_32_out, not_33_out, not_34_out,
       not_35_out, not_36_out, not_37_out, not_38_out, not_39_out, not_40_out, not_41_out, not_42_out;
  wire [4:0] demultiplexer_1_out0, demultiplexer_1_out1;

  Demultiplexer #(.width(5)) demultiplexer_1 (
    .out0(demultiplexer_1_out0), .out1(demultiplexer_1_out1), .in(opcode[4:0]), .sel(opcode[5]));  // open: en
  Demultiplexer #(.select(5)) demultiplexer_2 (
    .out0(demultiplexer_2_out0), .out2(Jump), .out4(BEQ), .out5(BNE), .out8(demultiplexer_2_out8),
    .out10(demultiplexer_2_out10), .out12(demultiplexer_2_out12), .out13(demultiplexer_2_out13),
    .out14(demultiplexer_2_out14), .in(1'b1), .sel(demultiplexer_1_out0));  // open: out1, out3, out6, out7, out9, out11, out15, out16, out17, out18, out19, out20, out21, out22, out23, out24, out25, out26, out27, out28, out29, out30, out31, en
  Demultiplexer #(.select(5)) demultiplexer_3 (
    .out3(demultiplexer_3_out3), .out11(demultiplexer_3_out11), .in(1'b1), .sel(demultiplexer_1_out1));  // open: out0, out1, out2, out4, out5, out6, out7, out8, out9, out10, out12, out13, out14, out15, out16, out17, out18, out19, out20, out21, out22, out23, out24, out25, out26, out27, out28, out29, out30, out31, en
  not not_1 (not_1_out, demultiplexer_2_out14);
  not not_2 (not_2_out, demultiplexer_3_out3);
  not not_3 (not_3_out, demultiplexer_2_out8);
  not not_4 (not_4_out, demultiplexer_2_out10);
  not not_5 (not_5_out, demultiplexer_2_out12);
  not not_6 (not_6_out, demultiplexer_2_out13);
  _6bit_multiplexer u_6bit_multiplexer_1 (
    .R_Type(demultiplexer_2_out0), .jump(Jump), .beq(BEQ), .bne(BNE), .Addi(not_3_out), .slti(not_4_out),
    .andi(not_5_out), .ori(not_6_out), .xori(not_1_out), .load(not_2_out), .store(demultiplexer_3_out11),
    .Bit_1_5(opcode[4:0]), .Bit_6(opcode[5]), .\output (RegDst));
  not not_7 (not_7_out, demultiplexer_3_out11);
  not not_8 (not_8_out, Jump);
  not not_9 (not_9_out, BEQ);
  not not_10 (not_10_out, BNE);
  _6bit_multiplexer u_6bit_multiplexer_2 (
    .R_Type(demultiplexer_2_out0), .jump(not_8_out), .beq(not_9_out), .bne(not_10_out),
    .Addi(demultiplexer_2_out8), .slti(demultiplexer_2_out10), .andi(demultiplexer_2_out12),
    .ori(demultiplexer_2_out13), .xori(demultiplexer_2_out14), .load(demultiplexer_3_out3),
    .store(not_7_out), .Bit_1_5(opcode[4:0]), .Bit_6(opcode[5]), .\output (RegWrite));
  not not_11 (not_11_out, demultiplexer_2_out12);
  not not_12 (not_12_out, demultiplexer_2_out13);
  not not_13 (not_13_out, demultiplexer_2_out14);
  _6bit_multiplexer u_6bit_multiplexer_3 (
    .R_Type(demultiplexer_2_out0), .jump(Jump), .beq(BEQ), .bne(BNE), .Addi(demultiplexer_2_out8),
    .slti(demultiplexer_2_out10), .andi(not_11_out), .ori(not_12_out), .xori(not_13_out),
    .load(demultiplexer_3_out3), .store(demultiplexer_3_out11), .Bit_1_5(opcode[4:0]), .Bit_6(opcode[5]),
    .\output (ExtOp));
  not not_14 (not_14_out, BNE);
  _6bit_multiplexer u_6bit_multiplexer_4 (
    .R_Type(not_15_out), .jump(Jump), .beq(not_16_out), .bne(not_14_out), .Addi(demultiplexer_2_out8),
    .slti(demultiplexer_2_out10), .andi(demultiplexer_2_out12), .ori(demultiplexer_2_out13),
    .xori(demultiplexer_2_out14), .load(demultiplexer_3_out3), .store(demultiplexer_3_out11),
    .Bit_1_5(opcode[4:0]), .Bit_6(opcode[5]), .\output (ALUSrc));
  not not_15 (not_15_out, demultiplexer_2_out0);
  not not_16 (not_16_out, BEQ);
  not not_17 (not_17_out, demultiplexer_2_out12);
  not not_18 (not_18_out, demultiplexer_2_out13);
  not not_19 (not_19_out, demultiplexer_2_out14);
  not not_20 (not_20_out, demultiplexer_2_out10);
  not not_21 (not_21_out, demultiplexer_3_out11);
  _6bit_multiplexer u_6bit_multiplexer_5 (
    .R_Type(not_22_out), .jump(not_23_out), .beq(not_24_out), .bne(not_25_out), .Addi(not_26_out),
    .slti(not_20_out), .andi(not_17_out), .ori(not_18_out), .xori(not_19_out), .load(demultiplexer_3_out3),
    .store(not_21_out), .Bit_1_5(opcode[4:0]), .Bit_6(opcode[5]), .\output (MemRd));
  not not_22 (not_22_out, demultiplexer_2_out0);
  not not_23 (not_23_out, Jump);
  not not_24 (not_24_out, BEQ);
  not not_25 (not_25_out, BNE);
  not not_26 (not_26_out, demultiplexer_2_out8);
  not not_27 (not_27_out, demultiplexer_2_out12);
  not not_28 (not_28_out, demultiplexer_2_out13);
  not not_29 (not_29_out, demultiplexer_2_out14);
  not not_30 (not_30_out, demultiplexer_3_out3);
  not not_31 (not_31_out, demultiplexer_2_out0);
  not not_32 (not_32_out, Jump);
  not not_33 (not_33_out, BEQ);
  not not_34 (not_34_out, BNE);
  not not_35 (not_35_out, demultiplexer_2_out8);
  not not_36 (not_36_out, demultiplexer_2_out10);
  _6bit_multiplexer u_6bit_multiplexer_6 (
    .R_Type(not_31_out), .jump(not_32_out), .beq(not_33_out), .bne(not_34_out), .Addi(not_35_out),
    .slti(not_36_out), .andi(not_27_out), .ori(not_28_out), .xori(not_29_out), .load(not_30_out),
    .store(demultiplexer_3_out11), .Bit_1_5(opcode[4:0]), .Bit_6(opcode[5]), .\output (MemWr));
  not not_37 (not_37_out, demultiplexer_2_out14);
  not not_38 (not_38_out, demultiplexer_2_out12);
  not not_39 (not_39_out, demultiplexer_2_out0);
  not not_40 (not_40_out, demultiplexer_2_out13);
  not not_41 (not_41_out, demultiplexer_2_out8);
  not not_42 (not_42_out, demultiplexer_2_out10);
  _6bit_multiplexer u_6bit_multiplexer_7 (
    .R_Type(not_39_out), .jump(Jump), .beq(BEQ), .bne(BNE), .Addi(not_41_out), .slti(not_42_out),
    .andi(not_38_out), .ori(not_40_out), .xori(not_37_out), .load(demultiplexer_3_out3),
    .store(demultiplexer_3_out11), .Bit_1_5(opcode[4:0]), .Bit_6(opcode[5]), .\output (MemtoReg));
endmodule

module _6bit_multiplexer (
  input  R_Type,
  input  jump,
  input  beq,
  input  bne,
  input  Addi,
  input  slti,
  input  andi,
  input  ori,
  input  xori,
  input  Bit_6,
  input  load,
  input  store,
  input  [4:0] Bit_1_5,
  output \output 
);

  wire multiplexer_1_out, multiplexer_2_out;

  Multiplexer #(.select(5)) multiplexer_1 (
    .in0(R_Type), .in2(jump), .in4(beq), .in5(bne), .in8(Addi), .in10(slti), .in12(andi), .in13(ori),
    .in14(xori), .out(multiplexer_1_out), .sel(Bit_1_5));  // open: in1, in3, in6, in7, in9, in11, in15, in16, in17, in18, in19, in20, in21, in22, in23, in24, in25, in26, in27, in28, in29, in30, in31, en
  Multiplexer #(.select(5)) multiplexer_2 (
    .in3(load), .in11(store), .out(multiplexer_2_out), .sel(Bit_1_5));  // open: in0, in1, in2, in4, in5, in6, in7, in8, in9, in10, in12, in13, in14, in15, in16, in17, in18, in19, in20, in21, in22, in23, in24, in25, in26, in27, in28, in29, in30, in31, en
  Multiplexer multiplexer_3 (
    .in0(multiplexer_1_out), .in1(multiplexer_2_out), .out(\output ), .sel(Bit_6));  // open: en
endmodule

module PC_Control (
  input  Jump,
  input  Zero,
  input  BNE,
  input  BEQ,
  output [1:0] Select_Bits
);

  wire and_1_out, and_2_out, not_1_out;

  not not_1 (not_1_out, Zero);
  or or_1 (Select_Bits[1], and_1_out, and_2_out);
  and and_1 (and_1_out, not_1_out, BNE);
  and and_2 (and_2_out, Zero, BEQ);

  assign Select_Bits[0] = Jump;
endmodule

module ALU_Control (
  input  [5:0] opcode,
  input  [5:0] \function ,
  output [3:0] ALU_Control
);

  wire demultiplexer_2_out0, not_39_out;
  wire [3:0] demultiplexer_2_out12, demultiplexer_4_out4, multiplexer_1_out, n4bit_6bit_multiplexer_1_output,
       not_4_out, not_18_out, not_21_out, not_22_out, not_27_out, not_29_out, not_35_out, not_38_out;
  wire [3:1] demultiplexer_2_out14, demultiplexer_4_out6, not_5_out, not_6_out, not_9_out;
  wire [4:0] demultiplexer_1_out0, demultiplexer_1_out1;

  Demultiplexer #(.width(5)) demultiplexer_1 (
    .out0(demultiplexer_1_out0), .out1(demultiplexer_1_out1), .in(opcode[4:0]), .sel(opcode[5]));  // open: en
  Demultiplexer #(.select(5)) demultiplexer_2 (
    .out0(demultiplexer_2_out0), .out4(not_5_out[2]), .out5(not_9_out[2]), .out8(not_18_out[2]),
    .out10(not_22_out[2]), .out12(demultiplexer_2_out12[0]), .out13(not_29_out[1]),
    .out14(demultiplexer_2_out14[1]), .in(1'b1), .sel(demultiplexer_1_out0));  // open: out1, out2, out3, out6, out7, out9, out11, out15, out16, out17, out18, out19, out20, out21, out22, out23, out24, out25, out26, out27, out28, out29, out30, out31, en
  Demultiplexer #(.select(5)) demultiplexer_3 (
    .out3(not_35_out[2]), .out11(not_38_out[2]), .in(1'b1), .sel(demultiplexer_1_out1));  // open: out0, out1, out2, out4, out5, out6, out7, out8, out9, out10, out12, out13, out14, out15, out16, out17, out18, out19, out20, out21, out22, out23, out24, out25, out26, out27, out28, out29, out30, out31, en
  Demultiplexer #(.select(5)) demultiplexer_4 (
    .out0(not_4_out[2]), .out2(not_6_out[2]), .out4(demultiplexer_4_out4[0]), .out5(not_21_out[1]),
    .out6(demultiplexer_4_out6[1]), .out10(not_27_out[2]), .in(1'b1), .sel(\function [4:0]));  // open: out1, out3, out7, out8, out9, out11, out12, out13, out14, out15, out16, out17, out18, out19, out20, out21, out22, out23, out24, out25, out26, out27, out28, out29, out30, out31, en
  not not_1 (not_4_out[3], not_4_out[2]);
  not not_2 (not_5_out[3], not_5_out[2]);
  not not_3 (not_4_out[1], not_4_out[2]);
  not not_4 (not_4_out[0], not_4_out[2]);
  not not_5 (not_5_out[1], not_5_out[2]);
  not not_6 (not_6_out[1], not_6_out[2]);
  not not_7 (not_6_out[3], not_6_out[2]);
  not not_8 (not_9_out[3], not_9_out[2]);
  not not_9 (not_9_out[1], not_9_out[2]);
  not not_10 (demultiplexer_4_out4[3], demultiplexer_4_out4[0]);
  not not_11 (demultiplexer_4_out4[2], demultiplexer_4_out4[0]);
  not not_12 (demultiplexer_4_out4[1], demultiplexer_4_out4[0]);
  not not_13 (not_18_out[3], not_18_out[2]);
  not not_14 (not_21_out[2], not_21_out[1]);
  not not_15 (not_21_out[3], not_21_out[1]);
  not not_16 (not_22_out[3], not_22_out[2]);
  not not_17 (not_18_out[1], not_18_out[2]);
  not not_18 (not_18_out[0], not_18_out[2]);
  not not_19 (demultiplexer_4_out6[3], demultiplexer_4_out6[1]);
  not not_20 (demultiplexer_4_out6[2], demultiplexer_4_out6[1]);
  not not_21 (not_21_out[0], not_21_out[1]);
  not not_22 (not_22_out[0], not_22_out[2]);
  not not_23 (not_27_out[3], not_27_out[2]);
  not not_24 (demultiplexer_2_out12[3], demultiplexer_2_out12[0]);
  not not_25 (demultiplexer_2_out12[2], demultiplexer_2_out12[0]);
  not not_26 (demultiplexer_2_out12[1], demultiplexer_2_out12[0]);
  not not_27 (not_27_out[0], not_27_out[2]);
  not not_28 (not_29_out[3], not_29_out[1]);
  not not_29 (not_29_out[0], not_29_out[1]);
  not not_30 (not_29_out[2], not_29_out[1]);
  not not_31 (demultiplexer_2_out14[2], demultiplexer_2_out14[1]);
  not not_32 (demultiplexer_2_out14[3], demultiplexer_2_out14[1]);
  not not_33 (not_35_out[1], not_35_out[2]);
  not not_34 (not_35_out[3], not_35_out[2]);
  Multiplexer #(.select(5), .width(4)) multiplexer_1 (
    .in0(not_4_out), .in2({not_6_out, not_6_out[2]}), .in4(demultiplexer_4_out4), .in5(not_21_out),
    .in6({demultiplexer_4_out6, demultiplexer_4_out6[1]}),
    .in10({not_27_out[3:2], not_27_out[2], not_27_out[0]}), .out(multiplexer_1_out), .sel(\function [4:0]));  // open: in1, in3, in7, in8, in9, in11, in12, in13, in14, in15, in16, in17, in18, in19, in20, in21, in22, in23, in24, in25, in26, in27, in28, in29, in30, in31, en
  not not_35 (not_35_out[0], not_35_out[2]);
  not not_36 (not_38_out[1], not_38_out[2]);
  not not_37 (not_38_out[3], not_38_out[2]);
  not not_38 (not_38_out[0], not_38_out[2]);
  _4bit_6bit_Multiplexer u_4bit_6bit_multiplexer_1 (
    .beq({not_5_out, not_5_out[2]}), .bne({not_9_out, not_9_out[2]}), .Addi(not_18_out),
    .slti({not_22_out[3:2], not_22_out[2], not_22_out[0]}), .andi(demultiplexer_2_out12), .ori(not_29_out),
    .xori({demultiplexer_2_out14, demultiplexer_2_out14[1]}), .load(not_35_out), .store(not_38_out),
    .Bit_1_5(opcode[4:0]), .Bit_6(opcode[5]), .\output (n4bit_6bit_multiplexer_1_output));
  assign ALU_Control = not_39_out ? n4bit_6bit_multiplexer_1_output : 4'bz;  // Controlled_Buffer controlled_buffer_1
  not not_39 (not_39_out, demultiplexer_2_out0);
  assign ALU_Control = demultiplexer_2_out0 ? multiplexer_1_out : 4'bz;  // Controlled_Buffer controlled_buffer_2
endmodule

module _4bit_6bit_Multiplexer (
  input  [3:0] beq,
  input  [3:0] bne,
  input  [3:0] Addi,
  input  [3:0] slti,
  input  [3:0] andi,
  input  [3:0] ori,
  input  [3:0] xori,
  input  Bit_6,
  input  [3:0] load,
  input  [3:0] store,
  input  [4:0] Bit_1_5,
  output [3:0] \output 
);

  wire [3:0] multiplexer_1_out, multiplexer_2_out;

  Multiplexer #(.select(5), .width(4)) multiplexer_1 (
    .in4(beq), .in5(bne), .in8(Addi), .in10(slti), .in12(andi), .in13(ori), .in14(xori),
    .out(multiplexer_1_out), .sel(Bit_1_5));  // open: in0, in1, in2, in3, in6, in7, in9, in11, in15, in16, in17, in18, in19, in20, in21, in22, in23, in24, in25, in26, in27, in28, in29, in30, in31, en
  Multiplexer #(.select(5), .width(4)) multiplexer_2 (
    .in3(load), .in11(store), .out(multiplexer_2_out), .sel(Bit_1_5));  // open: in0, in1, in2, in4, in5, in6, in7, in8, in9, in10, in12, in13, in14, in15, in16, in17, in18, in19, in20, in21, in22, in23, in24, in25, in26, in27, in28, in29, in30, in31, en
  Multiplexer #(.width(4)) multiplexer_3 (
    .in0(multiplexer_1_out), .in1(multiplexer_2_out), .out(\output ), .sel(Bit_6));  // open: en
endmodule

module Data_Memory (
  input  [31:0] Address,
  input  MemWrite,
  input  Clock,
  input  MemRead,
  input  [31:0] Data_Input,
  output [31:0] Data_Output
);

  RAM #(.addrWidth(24), .dataWidth(32), .bus("separate")) ram_1 (
    .addr(Address[23:0]), .din(Data_Input), .data(Data_Output), .str(MemWrite), .clk(Clock), .ld(MemRead));  // open: sel, clr
endmodule
