// Logisim project Extender.circ as structural Verilog: 1 circuit, main circuit main
module main (
  input  [15:0] in_1,
  input  in_2,
  output [31:0] out_3
);

  wire [15:0] demultiplexer_1_out0, demultiplexer_1_out1;
  wire [31:0] bit_extender_1_out, bit_extender_2_out;

  Demultiplexer #(.width(16)) demultiplexer_1 (
    .out0(demultiplexer_1_out0), .out1(demultiplexer_1_out1), .in(in_1), .sel(in_2));  // open: en
  assign bit_extender_1_out = {{16{1'b0}}, demultiplexer_1_out0};  // Bit_Extender bit_extender_1
  assign bit_extender_2_out = {{16{demultiplexer_1_out1[15]}}, demultiplexer_1_out1};  // Bit_Extender bit_extender_2
  Multiplexer #(.width(32)) multiplexer_1 (
    .in0(bit_extender_1_out), .in1(bit_extender_2_out), .out(out_3), .sel(in_2));  // open: en
endmodule
