// Logisim project Logic Unit.circ as structural Verilog: 1 circuit, main circuit main
module main (
  input  in_1,
  input  [1:0] in_2
);

  wire [31:0] and_1_out, multiplexer_1_out, not_1_out, or_1_out, undriven, undriven_2, xor_1_out;

  assign and_1_out = undriven_2 & undriven;  // AND_Gate and_1, 32 bits wide
  assign or_1_out = undriven_2 | undriven;  // OR_Gate or_1, 32 bits wide
  assign xor_1_out = undriven_2 ^ undriven;  // XOR_Gate xor_1, 32 bits wide
  assign not_1_out = ~or_1_out;  // NOT_Gate not_1, 32 bits wide
  Multiplexer #(.select(2), .width(32)) multiplexer_1 (
    .in0(and_1_out), .in1(or_1_out), .in2(not_1_out), .in3(xor_1_out), .out(multiplexer_1_out), .sel(in_2),
    .en(in_1));
endmodule
