// Logisim project PCctrl.circ as structural Verilog: 1 circuit, main circuit main
module main (
  input  in_1,
  input  in_2,
  input  in_3,
  input  in_4,
  output [1:0] out_5
);

  wire and_1_out, and_2_out, not_1_out;

  not not_1 (not_1_out, in_2);
  or or_1 (out_5[1], and_1_out, and_2_out);
  and and_1 (and_1_out, not_1_out, in_3);
  and and_2 (and_2_out, in_2, in_4);

  assign out_5[0] = in_1;
endmodule
