// Logisim project Project.circ as structural Verilog: 3 circuits, main circuit main
module main (
  input  [31:0] in_1,
  input  [31:0] in_2,
  output [31:0] out_3
);

  or or_1 (out_3[0], in_1[0], in_2[0]);
  or or_2 (out_3[1], in_1[1], in_2[1]);
  or or_3 (out_3[2], in_1[2], in_2[2]);
  or or_4 (out_3[3], in_1[3], in_2[3]);
  or or_5 (out_3[4], in_1[4], in_2[4]);
  or or_6 (out_3[5], in_1[5], in_2[5]);
  or or_7 (out_3[6], in_1[6], in_2[6]);
  or or_8 (out_3[7], in_1[7], in_2[7]);
  or or_9 (out_3[8], in_1[8], in_2[8]);
  or or_10 (out_3[9], in_1[9], in_2[9]);
  or or_11 (out_3[10], in_1[10], in_2[10]);
  or or_12 (out_3[11], in_1[11], in_2[11]);
  or or_13 (out_3[12], in_1[12], in_2[12]);
  or or_14 (out_3[13], in_1[13], in_2[13]);
  or or_15 (out_3[14], in_1[14], in_2[14]);
  or or_16 (out_3[15], in_1[15], in_2[15]);
  or or_17 (out_3[16], in_1[16], in_2[16]);
  or or_18 (out_3[17], in_1[17], in_2[17]);
  or or_19 (out_3[18], in_1[18], in_2[18]);
  or or_20 (out_3[19], in_1[19], in_2[19]);
  or or_21 (out_3[20], in_1[20], in_2[20]);
  or or_22 (out_3[21], in_1[21], in_2[21]);
  or or_23 (out_3[22], in_1[22], in_2[22]);
  or or_24 (out_3[23], in_1[23], in_2[23]);
  or or_25 (out_3[24], in_1[24], in_2[24]);
  or or_26 (out_3[25], in_1[25], in_2[25]);
  or or_27 (out_3[26], in_1[26], in_2[26]);
  or or_28 (out_3[27], in_1[27], in_2[27]);
  or or_29 (out_3[28], in_1[28], in_2[28]);
  or or_30 (out_3[29], in_1[29], in_2[29]);
  or or_31 (out_3[30], in_1[30], in_2[30]);
  or or_32 (out_3[31], in_1[31], in_2[31]);

  // Notes on the sheet:
  //   A
  //   1
  //   5
  //   10
  //   15
  //   20
  //   25
  //   B
endmodule

module _32_bit_And_Gate (
  input  [31:0] in_1,
  input  [31:0] in_2,
  output [31:0] out_3
);

  or or_1 (out_3[0], in_1[0], in_2[0]);
  or or_2 (out_3[1], in_1[1], in_2[1]);
  or or_3 (out_3[2], in_1[2], in_2[2]);
  or or_4 (out_3[3], in_1[3], in_2[3]);
  or or_5 (out_3[4], in_1[4], in_2[4]);
  or or_6 (out_3[5], in_1[5], in_2[5]);
  or or_7 (out_3[6], in_1[6], in_2[6]);
  or or_8 (out_3[7], in_1[7], in_2[7]);
  or or_9 (out_3[8], in_1[8], in_2[8]);
  or or_10 (out_3[9], in_1[9], in_2[9]);
  or or_11 (out_3[10], in_1[10], in_2[10]);
  or or_12 (out_3[11], in_1[11], in_2[11]);
  or or_13 (out_3[12], in_1[12], in_2[12]);
  or or_14 (out_3[13], in_1[13], in_2[13]);
  or or_15 (out_3[14], in_1[14], in_2[14]);
  or or_16 (out_3[15], in_1[15], in_2[15]);
  or or_17 (out_3[16], in_1[16], in_2[16]);
  or or_18 (out_3[17], in_1[17], in_2[17]);
  or or_19 (out_3[18], in_1[18], in_2[18]);
  or or_20 (out_3[19], in_1[19], in_2[19]);
  or or_21 (out_3[20], in_1[20], in_2[20]);
  or or_22 (out_3[21], in_1[21], in_2[21]);
  or or_23 (out_3[22], in_1[22], in_2[22]);
  or or_24 (out_3[23], in_1[23], in_2[23]);
  or or_25 (out_3[24], in_1[24], in_2[24]);
  or or_26 (out_3[25], in_1[25], in_2[25]);
  or or_27 (out_3[26], in_1[26], in_2[26]);
  or or_28 (out_3[27], in_1[27], in_2[27]);
  or or_29 (out_3[28], in_1[28], in_2[28]);
  or or_30 (out_3[29], in_1[29], in_2[29]);
  or or_31 (out_3[30], in_1[30], in_2[30]);
  or or_32 (out_3[31], in_1[31], in_2[31]);

  // Notes on the sheet:
  //   1
  //   5
  //   10
  //   15
  //   20
  //   25
  //   B
endmodule

module Adder_Subtractor (
  input  [31:0] in_1
);

  Adder #(.width(1)) adder_1 (.a(in_1[0]));  // open: b, out, cin, cout

  // Notes on the sheet:
  //   A
endmodule
