// Logisim project registerFile.circ as structural Verilog: 1 circuit, main circuit main
module main (
  input  [4:0] RW,
  input  RegWrite,
  input  [31:0] BusW,
  input  [4:0] RA,
  input  [31:0] Zero,
  input  in_6,
  input  [4:0] RB,
  output [31:0] busA,
  output [31:0] busB
);

  wire and_1_out, and_2_out, and_3_out, and_4_out, and_5_out, and_6_out, and_7_out, and_8_out, and_9_out,
       and_10_out, and_11_out, and_12_out, and_13_out, and_14_out, and_15_out, and_16_out, and_17_out,
       and_18_out, and_19_out, and_20_out, and_21_out, and_22_out, and_23_out, and_24_out, and_25_out,
       and_26_out, and_27_out, and_28_out, and_29_out, and_30_out, and_31_out, clock_1_out, decoder_1_out1,
       decoder_1_out2, decoder_1_out3, decoder_1_out4, decoder_1_out5, decoder_1_out6, decoder_1_out7,
       decoder_1_out8, decoder_1_out9, decoder_1_out10, decoder_1_out11, decoder_1_out12, decoder_1_out13,
       decoder_1_out14, decoder_1_out15, decoder_1_out16, decoder_1_out17, decoder_1_out18, decoder_1_out19,
       decoder_1_out20, decoder_1_out21, decoder_1_out22, decoder_1_out23, decoder_1_out24, decoder_1_out25,
       decoder_1_out26, decoder_1_out27, decoder_1_out28, decoder_1_out29, decoder_1_out30, decoder_1_out31,
       decoder_2_out0, decoder_2_out1, decoder_2_out2, decoder_2_out3, decoder_2_out4, decoder_2_out5,
       decoder_2_out6, decoder_2_out7, decoder_2_out8, decoder_2_out9, decoder_2_out10, decoder_2_out11,
       decoder_2_out12, decoder_2_out13, decoder_2_out14, decoder_2_out15, decoder_2_out16, decoder_2_out17,
       decoder_2_out18, decoder_2_out19, decoder_2_out20, decoder_2_out21, decoder_2_out22, decoder_2_out23,
       decoder_2_out24, decoder_2_out25, decoder_2_out26, decoder_2_out27, decoder_2_out28, decoder_2_out29,
       decoder_2_out30, decoder_2_out31, decoder_3_out0, decoder_3_out1, decoder_3_out2, decoder_3_out3,
       decoder_3_out4, decoder_3_out5, decoder_3_out6, decoder_3_out7, decoder_3_out8, decoder_3_out9,
       decoder_3_out10, decoder_3_out11, decoder_3_out12, decoder_3_out13, decoder_3_out14, decoder_3_out15,
       decoder_3_out16, decoder_3_out17, decoder_3_out18, decoder_3_out19, decoder_3_out20, decoder_3_out21,
       decoder_3_out22, decoder_3_out23, decoder_3_out24, decoder_3_out25, decoder_3_out26, decoder_3_out27,
       decoder_3_out28, decoder_3_out29, decoder_3_out30, decoder_3_out31;
  wire [31:0] R1_q, R2_q, R3_q, R4_q, R5_q, R6_q, R7_q, R8_q, R9_q, R10_q, R11_q, R12_q, R13_q, R14_q, R15_q,
       R16_q, R17_q, R18_q, R19_q, R20_q, R21_q, R22_q, R23_q, R24_q, R25_q, R26_q, R27_q, R28_q, R30_q,
       R31_q;

  Decoder #(.select(5)) decoder_1 (
    .out1(decoder_1_out1), .out2(decoder_1_out2), .out3(decoder_1_out3), .out4(decoder_1_out4),
    .out5(decoder_1_out5), .out6(decoder_1_out6), .out7(decoder_1_out7), .out8(decoder_1_out8),
    .out9(decoder_1_out9), .out10(decoder_1_out10), .out11(decoder_1_out11), .out12(decoder_1_out12),
    .out13(decoder_1_out13), .out14(decoder_1_out14), .out15(decoder_1_out15), .out16(decoder_1_out16),
    .out17(decoder_1_out17), .out18(decoder_1_out18), .out19(decoder_1_out19), .out20(decoder_1_out20),
    .out21(decoder_1_out21), .out22(decoder_1_out22), .out23(decoder_1_out23), .out24(decoder_1_out24),
    .out25(decoder_1_out25), .out26(decoder_1_out26), .out27(decoder_1_out27), .out28(decoder_1_out28),
    .out29(decoder_1_out29), .out30(decoder_1_out30), .out31(decoder_1_out31), .sel(RW));  // open: out0, en
  Decoder #(.select(5)) decoder_2 (
    .out0(decoder_2_out0), .out1(decoder_2_out1), .out2(decoder_2_out2), .out3(decoder_2_out3),
    .out4(decoder_2_out4), .out5(decoder_2_out5), .out6(decoder_2_out6), .out7(decoder_2_out7),
    .out8(decoder_2_out8), .out9(decoder_2_out9), .out10(decoder_2_out10), .out11(decoder_2_out11),
    .out12(decoder_2_out12), .out13(decoder_2_out13), .out14(decoder_2_out14), .out15(decoder_2_out15),
    .out16(decoder_2_out16), .out17(decoder_2_out17), .out18(decoder_2_out18), .out19(decoder_2_out19),
    .out20(decoder_2_out20), .out21(decoder_2_out21), .out22(decoder_2_out22), .out23(decoder_2_out23),
    .out24(decoder_2_out24), .out25(decoder_2_out25), .out26(decoder_2_out26), .out27(decoder_2_out27),
    .out28(decoder_2_out28), .out29(decoder_2_out29), .out30(decoder_2_out30), .out31(decoder_2_out31),
    .sel(RA), .en(in_6));
  Decoder #(.select(5)) decoder_3 (
    .out0(decoder_3_out0), .out1(decoder_3_out1), .out2(decoder_3_out2), .out3(decoder_3_out3),
    .out4(decoder_3_out4), .out5(decoder_3_out5), .out6(decoder_3_out6), .out7(decoder_3_out7),
    .out8(decoder_3_out8), .out9(decoder_3_out9), .out10(decoder_3_out10), .out11(decoder_3_out11),
    .out12(decoder_3_out12), .out13(decoder_3_out13), .out14(decoder_3_out14), .out15(decoder_3_out15),
    .out16(decoder_3_out16), .out17(decoder_3_out17), .out18(decoder_3_out18), .out19(decoder_3_out19),
    .out20(decoder_3_out20), .out21(decoder_3_out21), .out22(decoder_3_out22), .out23(decoder_3_out23),
    .out24(decoder_3_out24), .out25(decoder_3_out25), .out26(decoder_3_out26), .out27(decoder_3_out27),
    .out28(decoder_3_out28), .out29(decoder_3_out29), .out30(decoder_3_out30), .out31(decoder_3_out31),
    .sel(RB), .en(in_6));
  and and_1 (and_1_out, RegWrite, decoder_1_out1);
  and and_2 (and_2_out, RegWrite, decoder_1_out3);
  and and_3 (and_3_out, RegWrite, decoder_1_out5);
  and and_4 (and_4_out, RegWrite, decoder_1_out7);
  and and_5 (and_5_out, RegWrite, decoder_1_out9);
  and and_6 (and_6_out, RegWrite, decoder_1_out11);
  and and_7 (and_7_out, RegWrite, decoder_1_out13);
  and and_8 (and_8_out, RegWrite, decoder_1_out15);
  and and_9 (and_9_out, RegWrite, decoder_1_out17);
  and and_10 (and_10_out, RegWrite, decoder_1_out19);
  and and_11 (and_11_out, RegWrite, decoder_1_out21);
  and and_12 (and_12_out, RegWrite, decoder_1_out23);
  and and_13 (and_13_out, RegWrite, decoder_1_out25);
  and and_14 (and_14_out, RegWrite, decoder_1_out27);
  and and_15 (and_15_out, RegWrite, decoder_1_out29);
  and and_16 (and_16_out, RegWrite, decoder_1_out31);
  assign busA = decoder_2_out0 ? Zero : 32'bz;  // Controlled_Buffer controlled_buffer_1
  and and_17 (and_17_out, RegWrite, decoder_1_out2);
  and and_18 (and_18_out, RegWrite, decoder_1_out4);
  and and_19 (and_19_out, RegWrite, decoder_1_out6);
  and and_20 (and_20_out, RegWrite, decoder_1_out8);
  and and_21 (and_21_out, RegWrite, decoder_1_out10);
  and and_22 (and_22_out, RegWrite, decoder_1_out12);
  and and_23 (and_23_out, RegWrite, decoder_1_out14);
  and and_24 (and_24_out, RegWrite, decoder_1_out16);
  and and_25 (and_25_out, RegWrite, decoder_1_out18);
  and and_26 (and_26_out, RegWrite, decoder_1_out20);
  and and_27 (and_27_out, RegWrite, decoder_1_out22);
  and and_28 (and_28_out, RegWrite, decoder_1_out24);
  and and_29 (and_29_out, RegWrite, decoder_1_out26);
  and and_30 (and_30_out, RegWrite, decoder_1_out28);
  and and_31 (and_31_out, RegWrite, decoder_1_out30);
  assign busB = decoder_3_out0 ? Zero : 32'bz;  // Controlled_Buffer controlled_buffer_2
  Clock clock_1 (.out(clock_1_out));
  Register #(.width(32)) R1 (.D(BusW), .en(and_1_out), .Q(R1_q), .clk(clock_1_out), .clr(1'b0));
  Register #(.width(32)) R2 (.D(BusW), .en(and_17_out), .Q(R2_q), .clk(clock_1_out), .clr(1'b0));
  Register #(.width(32)) R3 (.D(BusW), .en(and_2_out), .Q(R3_q), .clk(clock_1_out), .clr(1'b0));
  Register #(.width(32)) R4 (.D(BusW), .en(and_18_out), .Q(R4_q), .clk(clock_1_out), .clr(1'b0));
  Register #(.width(32)) R5 (.D(BusW), .en(and_3_out), .Q(R5_q), .clk(clock_1_out), .clr(1'b0));
  Register #(.width(32)) R6 (.D(BusW), .en(and_19_out), .Q(R6_q), .clk(clock_1_out), .clr(1'b0));
  Register #(.width(32)) R7 (.D(BusW), .en(and_4_out), .Q(R7_q), .clk(clock_1_out), .clr(1'b0));
  Register #(.width(32)) R8 (.D(BusW), .en(and_20_out), .Q(R8_q), .clk(clock_1_out), .clr(1'b0));
  Register #(.width(32)) R9 (.D(BusW), .en(and_5_out), .Q(R9_q), .clk(clock_1_out), .clr(1'b0));
  Register #(.width(32)) R10 (.D(BusW), .en(and_21_out), .Q(R10_q), .clk(clock_1_out), .clr(1'b0));
  Register #(.width(32)) R11 (.D(BusW), .en(and_6_out), .Q(R11_q), .clk(clock_1_out), .clr(1'b0));
  Register #(.width(32)) R12 (.D(BusW), .en(and_22_out), .Q(R12_q), .clk(clock_1_out), .clr(1'b0));
  Register #(.width(32)) R13 (.D(BusW), .en(and_7_out), .Q(R13_q), .clk(clock_1_out), .clr(1'b0));
  Register #(.width(32)) R14 (.D(BusW), .en(and_23_out), .Q(R14_q), .clk(clock_1_out), .clr(1'b0));
  Register #(.width(32)) R15 (.D(BusW), .en(and_8_out), .Q(R15_q), .clk(clock_1_out), .clr(1'b0));
  Register #(.width(32)) R16 (.D(BusW), .en(and_24_out), .Q(R16_q), .clk(clock_1_out), .clr(1'b0));
  Register #(.width(32)) R17 (.D(BusW), .en(and_9_out), .Q(R17_q), .clk(clock_1_out), .clr(1'b0));
  Register #(.width(32)) R0 (.clk(clock_1_out));  // open: D, en, Q, clr
  Register #(.width(32)) R18 (.D(BusW), .en(and_25_out), .Q(R18_q), .clk(clock_1_out), .clr(1'b0));
  Register #(.width(32)) R19 (.D(BusW), .en(and_10_out), .Q(R19_q), .clk(clock_1_out), .clr(1'b0));
  Register #(.width(32)) R20 (.D(BusW), .en(and_26_out), .Q(R20_q), .clk(clock_1_out), .clr(1'b0));
  Register #(.width(32)) R21 (.D(BusW), .en(and_11_out), .Q(R21_q), .clk(clock_1_out), .clr(1'b0));
  Register #(.width(32)) R22 (.D(BusW), .en(and_27_out), .Q(R22_q), .clk(clock_1_out), .clr(1'b0));
  Register #(.width(32)) R23 (.D(BusW), .en(and_12_out), .Q(R23_q), .clk(clock_1_out), .clr(1'b0));
  Register #(.width(32)) R24 (.D(BusW), .en(and_28_out), .Q(R24_q), .clk(clock_1_out), .clr(1'b0));
  Register #(.width(32)) R25 (.D(BusW), .en(and_13_out), .Q(R25_q), .clk(clock_1_out), .clr(1'b0));
  Register #(.width(32)) R26 (.D(BusW), .en(and_29_out), .Q(R26_q), .clk(clock_1_out), .clr(1'b0));
  Register #(.width(32)) R27 (.D(BusW), .en(and_14_out), .Q(R27_q), .clk(clock_1_out), .clr(1'b0));
  Register #(.width(32)) R28 (.D(BusW), .en(and_30_out), .Q(R28_q), .clk(clock_1_out), .clr(1'b0));
  Register #(.width(32)) R29 (.D(BusW), .en(and_15_out), .Q(R17_q), .clk(clock_1_out), .clr(1'b0));
  Register #(.width(32)) R30 (.D(BusW), .en(and_31_out), .Q(R30_q), .clk(clock_1_out), .clr(1'b0));
  Register #(.width(32)) R31 (.D(BusW), .en(and_16_out), .Q(R31_q), .clk(clock_1_out), .clr(1'b0));
  assign busA = decoder_2_out31 ? R31_q : 32'bz;  // Controlled_Buffer controlled_buffer_3
  assign busB = decoder_3_out31 ? R31_q : 32'bz;  // Controlled_Buffer controlled_buffer_4
  assign busA = decoder_2_out30 ? R30_q : 32'bz;  // Controlled_Buffer controlled_buffer_5
  assign busA = decoder_2_out29 ? R17_q : 32'bz;  // Controlled_Buffer controlled_buffer_6
  assign busB = decoder_3_out30 ? R30_q : 32'bz;  // Controlled_Buffer controlled_buffer_7
  assign busB = decoder_3_out29 ? R17_q : 32'bz;  // Controlled_Buffer controlled_buffer_8
  assign busB = decoder_3_out28 ? R28_q : 32'bz;  // Controlled_Buffer controlled_buffer_9
  assign busA = decoder_2_out28 ? R28_q : 32'bz;  // Controlled_Buffer controlled_buffer_10
  assign busA = decoder_2_out27 ? R27_q : 32'bz;  // Controlled_Buffer controlled_buffer_11
  assign busB = decoder_3_out27 ? R27_q : 32'bz;  // Controlled_Buffer controlled_buffer_12
  assign busA = decoder_2_out26 ? R26_q : 32'bz;  // Controlled_Buffer controlled_buffer_13
  assign busB = decoder_3_out26 ? R26_q : 32'bz;  // Controlled_Buffer controlled_buffer_14
  assign busA = decoder_2_out25 ? R25_q : 32'bz;  // Controlled_Buffer controlled_buffer_15
  assign busB = decoder_3_out25 ? R25_q : 32'bz;  // Controlled_Buffer controlled_buffer_16
  assign busA = decoder_2_out24 ? R24_q : 32'bz;  // Controlled_Buffer controlled_buffer_17
  assign busB = decoder_3_out24 ? R24_q : 32'bz;  // Controlled_Buffer controlled_buffer_18
  assign busA = decoder_2_out23 ? R23_q : 32'bz;  // Controlled_Buffer controlled_buffer_19
  assign busB = decoder_3_out23 ? R23_q : 32'bz;  // Controlled_Buffer controlled_buffer_20
  assign busA = decoder_2_out22 ? R22_q : 32'bz;  // Controlled_Buffer controlled_buffer_21
  assign busB = decoder_3_out22 ? R22_q : 32'bz;  // Controlled_Buffer controlled_buffer_22
  assign busA = decoder_2_out21 ? R21_q : 32'bz;  // Controlled_Buffer controlled_buffer_23
  assign busA = decoder_2_out20 ? R20_q : 32'bz;  // Controlled_Buffer controlled_buffer_24
  assign busB = decoder_3_out21 ? R21_q : 32'bz;  // Controlled_Buffer controlled_buffer_25
  assign busB = decoder_3_out20 ? R20_q : 32'bz;  // Controlled_Buffer controlled_buffer_26
  assign busA = decoder_2_out19 ? R19_q : 32'bz;  // Controlled_Buffer controlled_buffer_27
  assign busA = decoder_2_out18 ? R18_q : 32'bz;  // Controlled_Buffer controlled_buffer_28
  assign busB = decoder_3_out19 ? R19_q : 32'bz;  // Controlled_Buffer controlled_buffer_29
  assign busB = decoder_3_out18 ? R18_q : 32'bz;  // Controlled_Buffer controlled_buffer_30
  assign busA = decoder_2_out17 ? R17_q : 32'bz;  // Controlled_Buffer controlled_buffer_31
  assign busB = decoder_3_out17 ? R17_q : 32'bz;  // Controlled_Buffer controlled_buffer_32
  assign busA = decoder_2_out16 ? R16_q : 32'bz;  // Controlled_Buffer controlled_buffer_33
  assign busB = decoder_3_out16 ? R16_q : 32'bz;  // Controlled_Buffer controlled_buffer_34
  assign busA = decoder_2_out15 ? R15_q : 32'bz;  // Controlled_Buffer controlled_buffer_35
  assign busA = decoder_2_out14 ? R14_q : 32'bz;  // Controlled_Buffer controlled_buffer_36
  assign busB = decoder_3_out15 ? R15_q : 32'bz;  // Controlled_Buffer controlled_buffer_37
  assign busB = decoder_3_out14 ? R14_q : 32'bz;  // Controlled_Buffer controlled_buffer_38
  assign busB = decoder_3_out13 ? R13_q : 32'bz;  // Controlled_Buffer controlled_buffer_39
  assign busA = decoder_2_out13 ? R13_q : 32'bz;  // Controlled_Buffer controlled_buffer_40
  assign busA = decoder_2_out12 ? R12_q : 32'bz;  // Controlled_Buffer controlled_buffer_41
  assign busA = decoder_2_out11 ? R11_q : 32'bz;  // Controlled_Buffer controlled_buffer_42
  assign busB = decoder_3_out12 ? R12_q : 32'bz;  // Controlled_Buffer controlled_buffer_43
  assign busB = decoder_3_out11 ? R11_q : 32'bz;  // Controlled_Buffer controlled_buffer_44
  assign busA = decoder_2_out10 ? R10_q : 32'bz;  // Controlled_Buffer controlled_buffer_45
  assign busA = decoder_2_out9 ? R9_q : 32'bz;  // Controlled_Buffer controlled_buffer_46
  assign busB = decoder_3_out10 ? R10_q : 32'bz;  // Controlled_Buffer controlled_buffer_47
  assign busB = decoder_3_out9 ? R9_q : 32'bz;  // Controlled_Buffer controlled_buffer_48
  assign busB = decoder_3_out8 ? R8_q : 32'bz;  // Controlled_Buffer controlled_buffer_49
  assign busA = decoder_2_out8 ? R8_q : 32'bz;  // Controlled_Buffer controlled_buffer_50
  assign busA = decoder_2_out7 ? R7_q : 32'bz;  // Controlled_Buffer controlled_buffer_51
  assign busB = decoder_3_out7 ? R7_q : 32'bz;  // Controlled_Buffer controlled_buffer_52
  assign busA = decoder_2_out6 ? R6_q : 32'bz;  // Controlled_Buffer controlled_buffer_53
  assign busA = decoder_2_out5 ? R5_q : 32'bz;  // Controlled_Buffer controlled_buffer_54
  assign busB = decoder_3_out6 ? R6_q : 32'bz;  // Controlled_Buffer controlled_buffer_55
  assign busB = decoder_3_out5 ? R5_q : 32'bz;  // Controlled_Buffer controlled_buffer_56
  assign busA = decoder_2_out4 ? R4_q : 32'bz;  // Controlled_Buffer controlled_buffer_57
  assign busB = decoder_3_out4 ? R4_q : 32'bz;  // Controlled_Buffer controlled_buffer_58
  assign busA = decoder_2_out3 ? R3_q : 32'bz;  // Controlled_Buffer controlled_buffer_59
  assign busB = decoder_3_out3 ? R3_q : 32'bz;  // Controlled_Buffer controlled_buffer_60
  assign busA = decoder_2_out2 ? R2_q : 32'bz;  // Controlled_Buffer controlled_buffer_61
  assign busB = decoder_3_out2 ? R2_q : 32'bz;  // Controlled_Buffer controlled_buffer_62
  assign busA = decoder_2_out1 ? R1_q : 32'bz;  // Controlled_Buffer controlled_buffer_63
  assign busB = decoder_3_out1 ? R1_q : 32'bz;  // Controlled_Buffer controlled_buffer_64
endmodule
