// Logisim project shifter.circ as structural Verilog: 3 circuits, main circuit main
module main (
  input  [1:0] Shift_Operation,
  input  [31:0] Bus_A,
  input  [31:0] Bus_B,
  input  [1:0] ALU_Selection,
  input  Arithmetic_Operation,
  input  [1:0] Logic_Operation,
  output [31:0] ALU_Result,
  output out_8
);

  wire adder_1_cout, comparator_1_lt;
  wire [31:0] adder_1_out, and_1_out, bit_extender_1_out, multiplexer_1_out, not_1_out, or_1_out,
       shifter_1_out_4, xor_1_out, xor_gate_1_output;

  assign and_1_out = Bus_A & Bus_B;  // AND_Gate and_1, 32 bits wide
  assign or_1_out = Bus_A | Bus_B;  // OR_Gate or_1, 32 bits wide
  assign xor_1_out = Bus_A ^ Bus_B;  // XOR_Gate xor_1, 32 bits wide
  shifter shifter_1 (.ShiftAmt(Bus_A[4:0]), .Input(Bus_A), .ShifterControl(Shift_Operation), .out_4(shifter_1_out_4));
  xor_gate xor_gate_1 (.BusB(Bus_B), .Control_Input(Arithmetic_Operation), .Output(xor_gate_1_output));
  Multiplexer #(.select(2), .width(32)) multiplexer_1 (
    .in0(and_1_out), .in1(or_1_out), .in2(not_1_out), .in3(xor_1_out), .out(multiplexer_1_out),
    .sel(Logic_Operation));  // open: en
  assign not_1_out = ~or_1_out;  // NOT_Gate not_1, 32 bits wide
  Comparator #(.width(1)) comparator_1 (.a(adder_1_out[31]), .b(adder_1_cout), .lt(comparator_1_lt));  // open: gt, eq
  Adder #(.width(32)) adder_1 (
    .a(Bus_A), .b(xor_gate_1_output), .out(adder_1_out), .cin(Arithmetic_Operation), .cout(adder_1_cout));
  assign bit_extender_1_out = {{31{1'b0}}, comparator_1_lt};  // Bit_Extender bit_extender_1
  Multiplexer #(.select(2), .width(32)) multiplexer_2 (
    .in0(shifter_1_out_4), .in1(bit_extender_1_out), .in2(adder_1_out), .in3(multiplexer_1_out),
    .out(ALU_Result), .sel(ALU_Selection));  // open: en
  nor nor_1 (out_8, ALU_Result[31], ALU_Result[30], ALU_Result[29], ALU_Result[28], ALU_Result[27], ALU_Result[26], ALU_Result[25], ALU_Result[24], ALU_Result[23], ALU_Result[22], ALU_Result[21], ALU_Result[20], ALU_Result[19], ALU_Result[18], ALU_Result[17], ALU_Result[16], ALU_Result[15], ALU_Result[14], ALU_Result[13], ALU_Result[12], ALU_Result[11], ALU_Result[10], ALU_Result[9], ALU_Result[8], ALU_Result[7], ALU_Result[6], ALU_Result[5], ALU_Result[4], ALU_Result[3], ALU_Result[2], ALU_Result[1], ALU_Result[0]);
endmodule

module shifter (
  input  [4:0] ShiftAmt,
  input  [31:0] Input,
  input  [1:0] ShifterControl,
  output [31:0] out_4
);

  wire [31:0] shifter_1_out, shifter_2_out, shifter_3_out;

  Shifter #(.width(32)) shifter_1 (.in(Input), .\dist (ShiftAmt), .out(shifter_1_out));
  Shifter #(.width(32), .shift("lr")) shifter_2 (.in(Input), .\dist (ShiftAmt), .out(shifter_2_out));
  Shifter #(.width(32), .shift("ar")) shifter_3 (.in(Input), .\dist (ShiftAmt), .out(shifter_3_out));
  Multiplexer #(.select(2), .width(32)) multiplexer_1 (
    .in1(shifter_1_out), .in2(shifter_2_out), .in3(shifter_3_out), .out(out_4), .sel(ShifterControl));  // open: in0, en
endmodule

module xor_gate (
  input  [31:0] BusB,
  input  Control_Input,
  output [31:0] Output
);

  xor xor_1 (Output[0], BusB[0], Control_Input);
  xor xor_2 (Output[1], BusB[1], Control_Input);
  xor xor_3 (Output[2], BusB[2], Control_Input);
  xor xor_4 (Output[3], BusB[3], Control_Input);
  xor xor_5 (Output[4], BusB[4], Control_Input);
  xor xor_6 (Output[5], BusB[5], Control_Input);
  xor xor_7 (Output[6], BusB[6], Control_Input);
  xor xor_8 (Output[7], BusB[7], Control_Input);
  xor xor_9 (Output[8], BusB[8], Control_Input);
  xor xor_10 (Output[9], BusB[9], Control_Input);
  xor xor_11 (Output[10], BusB[10], Control_Input);
  xor xor_12 (Output[11], BusB[11], Control_Input);
  xor xor_13 (Output[12], BusB[12], Control_Input);
  xor xor_14 (Output[13], BusB[13], Control_Input);
  xor xor_15 (Output[14], BusB[14], Control_Input);
  xor xor_16 (Output[15], BusB[15], Control_Input);
  xor xor_17 (Output[16], BusB[16], Control_Input);
  xor xor_18 (Output[17], BusB[17], Control_Input);
  xor xor_19 (Output[18], BusB[18], Control_Input);
  xor xor_20 (Output[19], BusB[19], Control_Input);
  xor xor_21 (Output[20], BusB[20], Control_Input);
  xor xor_22 (Output[21], BusB[21], Control_Input);
  xor xor_23 (Output[22], BusB[22], Control_Input);
  xor xor_24 (Output[23], BusB[23], Control_Input);
  xor xor_25 (Output[24], BusB[24], Control_Input);
  xor xor_26 (Output[25], BusB[25], Control_Input);
  xor xor_27 (Output[26], BusB[26], Control_Input);
  xor xor_28 (Output[27], BusB[27], Control_Input);
  xor xor_29 (Output[28], BusB[28], Control_Input);
  xor xor_30 (Output[29], BusB[29], Control_Input);
  xor xor_31 (Output[30], BusB[30], Control_Input);
  xor xor_32 (Output[31], BusB[31], Control_Input);

  // Notes on the sheet:
  //   1
  //   5
  //   10
  //   15
  //   20
  //   25
endmodule
